// Digital circuit NuPDP.dig as structural Verilog
module NuPDP (
  input  MAX,
  input  [11:0] SWITCH,
  input  _25Hz,
  input  [11:0] in_4,
  input  in_5,
  input  _1Hz,
  input  clk
);

  wire _2_out, _74ls161_1_rco, _74ls161_2_rco, _74ls273_7_q0, _74ls273_7_q1, _74ls273_7_q2, _74ls273_7_q3,
       _74ls273_7_q4, _74ls273_7_q5, _74ls273_7_q6, _74ls273_7_q7, _74ls273_8_q0, _74ls273_8_q1,
       _74ls273_8_q2, _74ls273_8_q3, _74ls283_1_c_out, _74ls283_1_s1, _74ls283_1_s2, _74ls283_1_s3,
       _74ls283_1_s4, _74ls283_2_c_out, _74ls283_2_s1, _74ls283_2_s2, _74ls283_2_s3, _74ls283_2_s4,
       _74ls283_3_s1, _74ls283_3_s2, _74ls283_3_s3, _74ls283_3_s4, _74ls283_4_c_out, _74ls283_4_s1,
       _74ls283_4_s2, _74ls283_4_s3, _74ls283_4_s4, _74ls283_5_c_out, _74ls283_5_s1, _74ls283_5_s2,
       _74ls283_5_s3, _74ls283_5_s4, _74ls283_6_s1, _74ls283_6_s2, _74ls283_6_s3, _74ls283_6_s4, aiFinished,
       ALU_Lin, ALU_Lout, AND, and_1_out, and_2_out, and_3_out, and_4_out, and_5_out, and_6_out, and_8_out,
       and_10_out, and_11_out, and_12_out, and_25_out, and_26_out, and_27_out, and_28_out, and_29_out,
       and_30_out, and_31_out, and_32_out, and_33_out, and_34_out, and_35_out, and_36_out, and_46_out,
       and_50_out, and_51_out, and_52_out, and_53_out, and_59_out, and_60_out, and_64_out, and_69_out,
       and_95_out, and_99_out, and_100_out, and_101_out, and_102_out, and_103_out, and_104_out, and_105_out,
       and_106_out, and_107_out, and_113_out, and_116_out, and_117_out, and_119_out, and_120_out,
       and_122_out, and_123_out, and_124_out, and_126_out, and_128_out, and_129_out, and_131_out,
       and_132_out, and_135_out, and_138_out, and_143_out, and_144_out, and_147_out, and_148_out, AND_TAD_d3,
       AND_TAD_d4, AND_TAD_d5, AND_TAD_d6, AND_TAD_p1, AND_TAD_p2, AND_TAD_p3, AND_TAD_p4, AND_TAD_p5,
       AND_TAD_p6, AND_TAD_p7, BP, BSW, CAF, CAF_6007, ckACC_2, ckACC_4, ckACC_5, ckACC_gtf, ckACC_iot1,
       ckACC_mop1, ckACC_mop2, ckDBUStoABUS_andtad, ckDBUStoABUS_dca, ckDBUStoABUS_isz, ckDBUStoABUS_jmp,
       ckDBUStoABUS_jms, ckIncDBUS__ai, ckIncDBUS__isz2, ckIncDBUS_isz1, ckIncPC_irq1, ckIncPC_jms1,
       ckIncPC_LoadIR, ckIR_0, ckIR_irq, ckIR_LoadIR, ckIRQhandler, ckMQ_1, ckSetPC_0, ckSetPC_jmp,
       ckSetPC_jms, CLA, CLA_1, CLA_2, CLA_3, CLA_4, CLK_t, CLL, clrPC_irq, CMA, CML, CODE_lsb, CODE_mid,
       CODE_msb, comparator_1_eq, d_ff_2_q, d_ff_3_nq, d_ff_as_1_q, d_ff_as_2_nq, d_ff_as_2_q, DCA, DCA_d1,
       DCA_d2, DCA_d3, DCA_d4, DCA_d5, DCA_p1, DCA_p2, DCA_p3, DCA_p4, DCA_p5, DCA_p7, delay_3_out,
       enACCclear_dca, enACCclear_iot1, enACCclear_mop3a, enACCclear_mop3b, enACCclear_mop3c,
       enACCclear_mop3d, enACCtoABUS, enACCtoDBUS_2, enACCtoDBUS_dca, enALUadd, enALUand, enALUor_mop2,
       enALUtoACC_andtad, enALUtoACC_mop1, enALUtoACC_mop2, enDBUStoABUS_andtad, enDBUStoABUS_dca,
       enIncToDBUS_ai, enIncToDBUS_isz1, enIncToDBUS_isz2, enINSTRtoABUS_ai, enINSTRtoABUS_andtad,
       enINSTRtoABUS_dca, enINSTRtoABUS_isz, enINSTRtoABUS_jmp, enINSTRtoABUS_jms, enIRQ, enMQclear,
       enPCtoABUS_0, enPCtoABUS_irq, enPCtoABUS_LoadIR, enPCtoABUS_mop2, enPCtoDBUS_irq, enRAMtoDBUS_ai,
       enRAMtoDBUS_andtad, enRAMtoDBUS_dca, enRAMtoDBUS_isz, enRAMtoDBUS_jmp, enRAMtoDBUS_jms, fAccZero,
       fAutoinc, fDBUSisZero, fGIE, fIndirect, fIrqDly, fKBD, fPendInt, fPRN, fSkip, GTF_6004, H_out, HLT,
       IAC, IAC_carryout, iDone, iDone1, iDoneBeforeIRQ, ii, ii_dca, ii_iot, ii_isz, ii_jmp, ii_jms, ii_mop1,
       ii_mop2, ii_mop3a, ii_mop3b, ii_mop3c, ii_mop3d, INC1, INC1_iot, INC1_isz, INC1_mop2, INC1_mop3a,
       INC1_mop3b, INC1_mop3c, INC1_mop3d, INC2, INC2_iot1, INC2_iot2, INC2_iot3, INC2_iot4, INC2_iot5,
       INC2_isz, INC2_mop2, INDIRECT, inhibitIR, INTE_nq, IOF_6002, ION_6001, IOT, IOT_CPU, IOT_d1, IOT_d2,
       IOT_d3, IOT_d4, IOT_d5, IOT_d6, IOT_d7, IOT_HISPEEDPUNCH, IOT_HISPEEDREADER, IOT_p2, IOT_p3, IOT_p4,
       IOT_p5, IOT_p6, IOT_TTYPUNCH, IOT_TTYREADER, isCurrPage, ISZ, ISZ_ISZi_d1, ISZ_ISZi_d4, ISZ_ISZi_p1,
       ISZ_ISZi_p2, ISZ_ISZi_p3, JMP, JMP_JMPi_d2, JMP_JMPi_d3, JMP_JMPi_d4, JMP_JMPi_d5, JMP_JMPi_d6,
       JMP_JMPi_p1, JMP_JMPi_p2, JMP_JMPi_p3, JMP_JMPi_p4, JMP_JMPi_p5, JMP_JMPi_p6, JMP_JMPi_p7, JMS,
       JMS_JMSi_d2, JMS_JMSi_d3, JMS_JMSi_d4, JMS_JMSi_d5, JMS_JMSi_d6, JMS_JMSi_d7, JMS_JMSi_p1,
       JMS_JMSi_p2, JMS_JMSi_p5, JMS_JMSi_p6, JMS_JMSi_p7, KCC_6032, KCF_6030, KIE, KIE_6035, KRB, KRB_6036,
       KRS_6034, KSF_6031, L1, L3, L4, L4b, L5, L6, L7, L9, LINK, M_out, MOP1, MOP1_d3, MOP1_d4, MOP1_d5,
       MOP1_d6, MOP1_d7, MOP1_p1, MOP1_p2, MOP1_p3, MOP1_p4, MOP1_p5, MOP1_p6, MOP2, MOP2_d2, MOP2_d4,
       MOP2_d5, MOP2_d6, MOP2_d7, MOP2_p1, MOP2_p3, MOP2_p4, MOP2_p5, MOP2_p6, MOP2_p7, MOP3, MOP3___MQA_p14,
       MOP3___MQA_p15, MOP3___MQL_d1, MOP3___MQL_d3, MOP3___MQL_d4, MOP3___MQL_d5, MOP3___MQL_d6,
       MOP3___MQL_d7, MOP3___MQL_p2, MOP3___MQL_p3, MOP3___MQL_p4, MOP3___MQL_p5, MOP3___MQL_p6,
       MOP3___MQL_p7, MOP3___NOP_CLR_d1, MOP3___NOP_CLR_d2, MOP3___NOP_CLR_d3, MOP3___NOP_CLR_d4,
       MOP3___NOP_CLR_d5, MOP3___NOP_CLR_d6, MOP3___NOP_CLR_d7, MOP3___NOP_CLR_p2, MOP3___NOP_CLR_p3,
       MOP3___NOP_CLR_p4, MOP3___NOP_CLR_p5, MOP3___NOP_CLR_p6, MOP3___NOP_CLR_p7, MOP3___SWP_d4,
       MOP3___SWP_d5, MOP3___SWP_d6, MOP3___SWP_d7, MOP3___SWP_p3, MOP3___SWP_p4, MOP3___SWP_p5,
       MOP3___SWP_p6, MOP3___SWP_p7, MQA, MQL, nand_1_out, nand_2_out, nand_3_out, nand_4_out, nand_5_out,
       nand_6_out, nor_1_out, nor_2_out, nor_3_out, not_1_out, not_3_out, not_4_out, not_5_out, not_6_out,
       not_7_out, not_8_out, not_9_out, not_10_out, not_11_out, not_12_out, not_13_out, not_14_out,
       not_15_out, not_16_out, not_18_out, not_20_out, not_21_out, not_22_out, not_23_out, not_24_out,
       not_25_out, not_26_out, not_27_out, not_28_out, not_30_out, not_31_out, not_32_out, not_33_out,
       not_34_out, not_35_out, not_36_out, not_37_out, not_38_out, not_39_out, not_40_out, not_41_out,
       not_42_out, not_43_out, not_45_out, oneshot_1_o, oneshot_2_o, oneshot_3_o, oneshot_4_o, oneshot_5_o,
       oneshot_6_o, oneshot_7_o, oneshot_8_o, oneshot_9_o, or_1_out, or_2_out, or_4_out, or_6_out, or_7_out,
       or_12_out, or_13_out, or_14_out, or_15_out, or_17_out, or_18_out, or_19_out, or_20_out, or_21_out,
       or_22_out, or_23_out, or_24_out, or_25_out, or_26_out, or_27_out, or_28_out, or_29_out, or_30_out,
       or_32_out, or_33_out, or_34_out, or_35_out, or_38_out, or_39_out, or_40_out, or_41_out, or_42_out,
       or_43_out, or_44_out, or_45_out, or_46_out, or_47_out, or_48_out, or_49_out, or_50_out, or_51_out,
       or_52_out, or_53_out, or_54_out, or_55_out, or_56_out, or_57_out, or_58_out, or_59_out, or_60_out,
       or_61_out, or_62_out, or_63_out, or_64_out, or_65_out, or_71_out, or_77_out, or_78_out, or_79_out,
       or_83_out, or_84_out, or_85_out, or_86_out, or_87_out, or_88_out, or_89_out, or_90_out, or_91_out,
       or_92_out, pulldown_14_out, R_out, reset_1_out, rs_ff_as_1_nq, rs_ff_as_1_q, rs_ff_as_2_q,
       rs_ff_as_3_q, rs_ff_as_5_q, rs_ff_as_6_q, RTF_INTEclr, RTF_INTEset, RTF_linkClr, RTF_linkSet, S_out,
       SCA, sequencer_1_d2, sequencer_1_d3, sequencer_1_d4, sequencer_1_d5, sequencer_1_d6, sequencer_1_d7,
       sequencer_1_p3, sequencer_1_p4, sequencer_1_p5, sequencer_1_p6, sequencer_1_p7, sequencer_2_d1,
       sequencer_2_d2, sequencer_2_d3, sequencer_2_d5, sequencer_2_d6, sequencer_2_d7, sequencer_2_p2,
       sequencer_2_p4, sequencer_2_p7, STOPSOON, t_ff_1_q, T_out, tty_1_rxavail, tty_1_txdone, TTY_IE_q,
       weRAM_ai, weRAM_dca, weRAM_irq, xor_1_out, xor_3_out, xor_4_out, xor_5_out, xor_6_out, xor_7_out,
       xor_8_out, xor_9_out, xor_10_out, xor_11_out, xor_12_out, xor_13_out, xor_14_out, ZEROPAGE;
  wire [3:0] and_13_out, and_17_out, and_21_out;
  wire [5:0] L_PRN;
  wire [5:2] L_IRQ;
  wire [7:1] L_CPU;
  wire [8:1] L_OPR2;
  wire [10:1] L_OPR1;
  wire [10:3] L_GEN;
  wire [11:0] ABUS, ACC, ALU_out, and_48_out, IR, IRA, MQ, OBUS, PC, ramspy_1_o, ramspy_2_o, ramspy_3_o,
       ramspy_4_o, ramspy_5_o;
  wire [12:0] L_OPR3;
  wire [15:0] CharRom3x_d, CharRom3x_d_2, CharRom3x_d_3;
  wire [19:0] counter_1_out, d_ff_1_q;
  wire [24:0] DAW;
  wire [50:50] CharRom3x_d_4;

  or or_1 (or_1_out, enIncToDBUS_isz1, enIncToDBUS_isz2, enIncToDBUS_ai);
  or or_2 (or_2_out, ckIncDBUS_isz1, ckIncDBUS__isz2, ckIncDBUS__ai);
  not not_1 (not_1_out, or_1_out);
  _74LS283 _74ls283_1 (
    .A1(DAW[0]), .A2(DAW[1]), .A3(DAW[2]), .A4(DAW[3]), .B1(1'b0), .B2(1'b0), .B3(1'b0), .B4(1'b0),
    .S1(_74ls283_1_s1), .S2(_74ls283_1_s2), .S3(_74ls283_1_s3), .S4(_74ls283_1_s4), .C_in(1'b1),
    .C_out(_74ls283_1_c_out));
  _74LS283 _74ls283_2 (
    .A1(DAW[4]), .A2(DAW[5]), .A3(DAW[6]), .A4(DAW[7]), .B1(1'b0), .B2(1'b0), .B3(1'b0), .B4(1'b0),
    .S1(_74ls283_2_s1), .S2(_74ls283_2_s2), .S3(_74ls283_2_s3), .S4(_74ls283_2_s4), .C_in(_74ls283_1_c_out),
    .C_out(_74ls283_2_c_out));
  _74LS283 _74ls283_3 (
    .A1(DAW[8]), .A2(DAW[9]), .A3(DAW[10]), .A4(DAW[11]), .B1(1'b0), .B2(1'b0), .B3(1'b0), .B4(1'b0),
    .S1(_74ls283_3_s1), .S2(_74ls283_3_s2), .S3(_74ls283_3_s3), .S4(_74ls283_3_s4), .C_in(_74ls283_2_c_out));  // open: C_out
  or or_3 (L7, enDBUStoABUS_andtad, ckDBUStoABUS_jmp, ckDBUStoABUS_jms, ckDBUStoABUS_isz, enDBUStoABUS_dca);
  or or_4 (or_4_out, ckDBUStoABUS_andtad, ckDBUStoABUS_jmp, ckDBUStoABUS_jms, ckDBUStoABUS_isz, ckDBUStoABUS_dca);
  not not_2 (L5, not_1_out);
  not not_3 (not_3_out, L7);
  not not_4 (not_4_out, L5);
  _74ls374 _74ls374_1 (
    .Q0(DAW[0]), .Q1(DAW[1]), .Q2(DAW[2]), .Q3(DAW[3]), .Q4(DAW[4]), .Q5(DAW[5]), .Q6(DAW[6]), .Q7(DAW[7]),
    .nOC(not_4_out), .CLK(or_2_out), .D0(_74ls283_1_s1), .D1(_74ls283_1_s2), .D2(_74ls283_1_s3),
    .D3(_74ls283_1_s4), .D4(_74ls283_2_s1), .D5(_74ls283_2_s2), .D6(_74ls283_2_s3), .D7(_74ls283_2_s4));  // open: iv
  _74ls374 _74ls374_2 (
    .Q0(DAW[8]), .Q1(DAW[9]), .Q2(DAW[10]), .Q3(DAW[11]), .nOC(not_4_out), .CLK(or_2_out),
    .D0(_74ls283_3_s1), .D1(_74ls283_3_s2), .D2(_74ls283_3_s3), .D3(_74ls283_3_s4), .D4(1'b0), .D5(1'b0),
    .D6(1'b0), .D7(1'b0));  // open: Q4, Q5, Q6, Q7, iv
  _74ls374 _74ls374_3 (
    .Q0(ABUS[0]), .Q1(ABUS[1]), .Q2(ABUS[2]), .Q3(ABUS[3]), .Q4(ABUS[4]), .Q5(ABUS[5]), .Q6(ABUS[6]),
    .Q7(ABUS[7]), .nOC(not_3_out), .CLK(or_4_out), .D0(DAW[0]), .D1(DAW[1]), .D2(DAW[2]), .D3(DAW[3]),
    .D4(DAW[4]), .D5(DAW[5]), .D6(DAW[6]), .D7(DAW[7]));  // open: iv
  _74ls374 _74ls374_4 (
    .Q0(ABUS[8]), .Q1(ABUS[9]), .Q2(ABUS[10]), .Q3(ABUS[11]), .nOC(not_3_out), .CLK(or_4_out), .D0(DAW[8]),
    .D1(DAW[9]), .D2(DAW[10]), .D3(DAW[11]), .D4(1'b0), .D5(1'b0), .D6(1'b0), .D7(1'b0));  // open: Q4, Q5, Q6, Q7, iv
  or or_5 (L3, enINSTRtoABUS_jmp, enINSTRtoABUS_andtad, enINSTRtoABUS_dca, enINSTRtoABUS_ai, enINSTRtoABUS_dca, enINSTRtoABUS_isz, enINSTRtoABUS_jms);
  Seven_Seg_Hex seven_seg_hex_1 (.d({1'b0, SWITCH[11:9]}), .dp(1'b0));
  LED led_1 (.in(L5));
  LED led_2 (.in(L7));
  Seven_Seg_Hex seven_seg_hex_2 (.d({1'b0, SWITCH[8:6]}), .dp(1'b0));
  and and_1 (and_1_out, PC[7], isCurrPage);
  and and_2 (and_2_out, PC[8], isCurrPage);
  and and_3 (and_3_out, PC[9], isCurrPage);
  and and_4 (and_4_out, PC[10], isCurrPage);
  and and_5 (and_5_out, PC[11], isCurrPage);
  Seven_Seg_Hex seven_seg_hex_3 (.d({1'b0, SWITCH[5:3]}), .dp(1'b0));
  not not_5 (not_5_out, L3);
  not not_6 (not_6_out, enALUor_mop2);
  Seven_Seg_Hex seven_seg_hex_4 (.d({1'b0, SWITCH[2:0]}), .dp(1'b0));
  _74LS244 _74ls244_1 (
    ._1A1(IR[0]), ._1A2(IR[1]), ._1A3(IR[2]), ._1A4(IR[3]), ._1nG(not_5_out), ._2A1(IR[4]), ._2A2(IR[5]),
    ._2A3(IR[6]), ._2A4(and_1_out), ._2nG(not_5_out), ._1Y1(ABUS[0]), ._1Y2(ABUS[1]), ._1Y3(ABUS[2]),
    ._1Y4(ABUS[3]), ._2Y1(ABUS[4]), ._2Y2(ABUS[5]), ._2Y3(ABUS[6]), ._2Y4(ABUS[7]));
  _74LS244 _74ls244_2 (
    ._1A1(and_2_out), ._1A2(and_3_out), ._1A3(and_4_out), ._1A4(and_5_out), ._1nG(not_5_out), ._2A1(1'b1),
    ._2A2(1'b1), ._2A3(1'b1), ._2A4(1'b1), ._2nG(1'b1), ._1Y1(ABUS[8]), ._1Y2(ABUS[9]), ._1Y3(ABUS[10]),
    ._1Y4(ABUS[11]));  // open: _2Y1, _2Y2, _2Y3, _2Y4
  // Probe on ABUS
  PullDown #(.Bits(12)) pulldown_1 (.out(ABUS));
  _74LS244 _74ls244_3 (
    ._1A1(SWITCH[0]), ._1A2(SWITCH[1]), ._1A3(SWITCH[2]), ._1A4(SWITCH[3]), ._1nG(not_6_out),
    ._2A1(SWITCH[4]), ._2A2(SWITCH[5]), ._2A3(SWITCH[6]), ._2A4(SWITCH[7]), ._2nG(not_6_out), ._1Y1(OBUS[0]),
    ._1Y2(OBUS[1]), ._1Y3(OBUS[2]), ._1Y4(OBUS[3]), ._2Y1(OBUS[4]), ._2Y2(OBUS[5]), ._2Y3(OBUS[6]),
    ._2Y4(OBUS[7]));
  _74LS244 _74ls244_4 (
    ._1A1(SWITCH[8]), ._1A2(SWITCH[9]), ._1A3(SWITCH[10]), ._1A4(SWITCH[11]), ._1nG(not_6_out), ._2A1(1'b1),
    ._2A2(1'b1), ._2A3(1'b1), ._2A4(1'b1), ._2nG(1'b1), ._1Y1(OBUS[8]), ._1Y2(OBUS[9]), ._1Y3(OBUS[10]),
    ._1Y4(OBUS[11]));  // open: _2Y1, _2Y2, _2Y3, _2Y4
  or or_6 (or_6_out, ckIncPC_LoadIR, ckIncPC_jms1, ckIncPC_irq1, 1'b0, 1'b0, not_7_out);
  or or_7 (or_7_out, ckSetPC_0, ckSetPC_jmp, ckSetPC_jms, 1'b0, 1'b0, 1'b0);
  or or_8 (L4, enPCtoABUS_0, enPCtoABUS_LoadIR, enPCtoABUS_mop2, enPCtoABUS_irq);
  or or_9 (L4b, ckIncPC_jms1, enPCtoDBUS_irq, 1'b0, 1'b0);
  or or_10 (DAW[24], weRAM_dca, enIncToDBUS_isz1, enIncToDBUS_isz2, weRAM_irq, ckIncPC_jms1, weRAM_ai);
  or or_11 (L6, ckSetPC_0, enPCtoABUS_LoadIR, enRAMtoDBUS_jmp, enRAMtoDBUS_jms, enPCtoABUS_irq, enRAMtoDBUS_andtad, enRAMtoDBUS_ai, enRAMtoDBUS_isz, enRAMtoDBUS_dca);
  LED led_3 (.in(L3));
  not not_7 (not_7_out, not_8_out);
  not not_8 (not_8_out, or_7_out);
  not not_9 (not_9_out, L4);
  not not_10 (not_10_out, L4b);
  Reset #(.invertOutput("false")) reset_1 (.out(reset_1_out));
  not not_11 (not_11_out, DAW[24]);
  not not_12 (not_12_out, L6);
  EEPROM #(.AddrBits(12), .isProgramMemory("true"), .Bits(12)) eeprom_1 (
    .A(ABUS), .CS(~reset_1_out), .WE(~not_11_out), .OE(~not_12_out), .D(DAW[11:0]));
  // Probe on DAW[11:0]
  or or_12 (or_12_out, DAW[0], DAW[1], DAW[2]);
  or or_13 (or_13_out, DAW[3], DAW[4], DAW[5]);
  or or_14 (or_14_out, DAW[6], DAW[7], DAW[8]);
  or or_15 (or_15_out, DAW[9], DAW[10], DAW[11]);
  PullDown pulldown_2 (.out(ABUS[2]));
  PullDown pulldown_3 (.out(ABUS[1]));
  PullDown pulldown_4 (.out(ABUS[3]));
  PullDown pulldown_5 (.out(ABUS[6]));
  PullDown pulldown_6 (.out(ABUS[5]));
  PullDown pulldown_7 (.out(ABUS[10]));
  PullDown pulldown_8 (.out(ABUS[9]));
  PullDown pulldown_9 (.out(ABUS[11]));
  not not_13 (not_13_out, clrPC_irq);
  or or_16 (L1, enACCtoDBUS_dca, enACCtoDBUS_2);
  or or_17 (or_17_out, enACCclear_dca, enACCclear_mop3a, enACCclear_mop3b, CAF_6007, enACCclear_mop3c, enACCclear_mop3d, enACCclear_iot1);
  not not_14 (not_14_out, or_17_out);
  // Probe on ALU_out
  or or_18 (or_18_out, ckACC_mop1, ckACC_2, ckACC_mop2, ckACC_gtf, ckACC_4, ckACC_5, ckACC_iot1);
  or or_19 (or_19_out, CAF_6007, RTF_linkClr);
  or or_20 (or_20_out, or_12_out, or_14_out, or_13_out);
  PullDown pulldown_10 (.out(ABUS[0]));
  PullDown pulldown_11 (.out(ABUS[4]));
  assign ABUS[7] = ckSetPC_0 ? 1'b1 : 1'bz;  // Driver driver_1
  PullDown pulldown_12 (.out(ABUS[8]));
  not not_15 (not_15_out, RTF_linkSet);
  not not_16 (not_16_out, or_19_out);
  LED led_4 (.in(L6));
  or or_21 (or_21_out, or_20_out, 1'b0, or_15_out);
  _74LS273 _74ls273_1 (
    .CP(or_18_out), .nMR(not_14_out), .D0(ALU_out[0]), .D1(ALU_out[1]), .D2(ALU_out[2]), .D3(ALU_out[3]),
    .D4(ALU_out[4]), .D5(ALU_out[5]), .D6(ALU_out[6]), .D7(ALU_out[7]), .Q0(ACC[0]), .Q1(ACC[1]),
    .Q2(ACC[2]), .Q3(ACC[3]), .Q4(ACC[4]), .Q5(ACC[5]), .Q6(ACC[6]), .Q7(ACC[7]));
  _74LS273 _74ls273_2 (
    .CP(or_18_out), .nMR(not_14_out), .D0(ALU_out[8]), .D1(ALU_out[9]), .D2(ALU_out[10]), .D3(ALU_out[11]),
    .D4(1'b0), .D5(1'b0), .D6(1'b0), .D7(1'b0), .Q0(ACC[8]), .Q1(ACC[9]), .Q2(ACC[10]), .Q3(ACC[11]));  // open: Q4, Q5, Q6, Q7
  _74LS74 _74ls74_1 (
    ._1nSD(not_15_out), ._1D(ALU_Lout), ._1CP(or_18_out), ._1nRD(not_16_out), ._2nSD(1'b1), ._2D(1'b1),
    ._2CP(1'b1), ._2nRD(1'b1), ._1Q(LINK));  // open: _1nQ, _2Q, _2nQ
  not not_17 (fDBUSisZero, or_21_out);
  _74LS161 _74ls161_1 (
    .CLK(or_6_out), .A(ABUS[0]), .B(ABUS[1]), .C(ABUS[2]), .D(ABUS[3]), .nLD(not_8_out), .nCLR(not_13_out),
    .ENT(1'b1), .ENP(1'b1), .QA(PC[0]), .QB(PC[1]), .QC(PC[2]), .QD(PC[3]), .RCO(_74ls161_1_rco));
  _74LS161 _74ls161_2 (
    .CLK(or_6_out), .A(ABUS[4]), .B(ABUS[5]), .C(ABUS[6]), .D(ABUS[7]), .nLD(not_8_out), .nCLR(not_13_out),
    .ENT(_74ls161_1_rco), .ENP(_74ls161_1_rco), .QA(PC[4]), .QB(PC[5]), .QC(PC[6]), .QD(PC[7]),
    .RCO(_74ls161_2_rco));
  _74LS161 _74ls161_3 (
    .CLK(or_6_out), .A(ABUS[8]), .B(ABUS[9]), .C(ABUS[10]), .D(ABUS[11]), .nLD(not_8_out), .nCLR(not_13_out),
    .ENT(_74ls161_2_rco), .ENP(_74ls161_2_rco), .QA(PC[8]), .QB(PC[9]), .QC(PC[10]), .QD(PC[11]));  // open: RCO
  PullDown pulldown_13 (.out(enACCtoABUS));
  // Probe PC on PC
  or or_22 (or_22_out, ACC[0], ACC[1], ACC[2]);
  or or_23 (or_23_out, ACC[3], ACC[4], ACC[5]);
  or or_24 (or_24_out, ACC[6], ACC[7], ACC[8]);
  or or_25 (or_25_out, ACC[9], ACC[10], ACC[11]);
  and and_6 (and_6_out, LINK, not_18_out);
  not not_18 (not_18_out, CLL);
  _74LS244 _74ls244_5 (
    ._1A1(PC[0]), ._1A2(PC[1]), ._1A3(PC[2]), ._1A4(PC[3]), ._1nG(not_9_out), ._2A1(PC[4]), ._2A2(PC[5]),
    ._2A3(PC[6]), ._2A4(PC[7]), ._2nG(not_9_out), ._1Y1(ABUS[0]), ._1Y2(ABUS[1]), ._1Y3(ABUS[2]),
    ._1Y4(ABUS[3]), ._2Y1(ABUS[4]), ._2Y2(ABUS[5]), ._2Y3(ABUS[6]), ._2Y4(ABUS[7]));
  _74LS244 _74ls244_6 (
    ._1A1(PC[8]), ._1A2(PC[9]), ._1A3(PC[10]), ._1A4(PC[11]), ._1nG(not_9_out), ._2A1(1'b1), ._2A2(1'b1),
    ._2A3(1'b1), ._2A4(1'b1), ._2nG(1'b1), ._1Y1(ABUS[8]), ._1Y2(ABUS[9]), ._1Y3(ABUS[10]), ._1Y4(ABUS[11]));  // open: _2Y1, _2Y2, _2Y3, _2Y4
  _74LS244 _74ls244_7 (
    ._1A1(PC[0]), ._1A2(PC[1]), ._1A3(PC[2]), ._1A4(PC[3]), ._1nG(not_10_out), ._2A1(PC[4]), ._2A2(PC[5]),
    ._2A3(PC[6]), ._2A4(PC[7]), ._2nG(not_10_out), ._1Y1(DAW[0]), ._1Y2(DAW[1]), ._1Y3(DAW[2]),
    ._1Y4(DAW[3]), ._2Y1(DAW[4]), ._2Y2(DAW[5]), ._2Y3(DAW[6]), ._2Y4(DAW[7]));
  _74LS244 _74ls244_8 (
    ._1A1(PC[8]), ._1A2(PC[9]), ._1A3(PC[10]), ._1A4(PC[11]), ._1nG(not_10_out), ._2A1(1'b1), ._2A2(1'b1),
    ._2A3(1'b1), ._2A4(1'b1), ._2nG(1'b1), ._1Y1(DAW[8]), ._1Y2(DAW[9]), ._1Y3(DAW[10]), ._1Y4(DAW[11]));  // open: _2Y1, _2Y2, _2Y3, _2Y4
  or or_26 (or_26_out, or_22_out, or_23_out, or_24_out);
  xor xor_1 (xor_1_out, and_6_out, CML);
  OneShot oneshot_1 (.i(_1Hz), .o(oneshot_1_o));
  or or_27 (or_27_out, or_26_out, 1'b0, or_25_out);
  T_FF t_ff_1 (.T(1'b1), .C(oneshot_1_o), .Q(t_ff_1_q));  // open: nQ
  not not_19 (fAccZero, or_27_out);
  xor xor_2 (ALU_Lin, xor_1_out, IAC_carryout);
  Counter #(.Bits(20)) counter_1 (.en(1'b1), .C(iDone), .clr(t_ff_1_q), .out(counter_1_out));  // open: ovf
  LED led_5 (.in(L4));
  LED led_6 (.in(L4b));
  D_FF #(.Bits(20)) d_ff_1 (.D(counter_1_out), .C(t_ff_1_q), .Q(d_ff_1_q));  // open: nQ
  not not_20 (not_20_out, L1);
  not not_21 (not_21_out, enACCtoABUS);
  PullUp pullup_1 (.out(not_21_out));
  // Probe on d_ff_1_q
  or or_28 (or_28_out, ckIR_0, ckIR_irq, ckIR_LoadIR);
  _74LS541 _74ls541_1 (
    .nOE1(not_20_out), .nOE2(not_20_out), ._0D(ACC[0]), ._1D(ACC[1]), ._2D(ACC[2]), ._3D(ACC[3]),
    ._4D(ACC[4]), ._5D(ACC[5]), ._6D(ACC[6]), ._7D(ACC[7]), ._0O(DAW[0]), ._1O(DAW[1]), ._2O(DAW[2]),
    ._3O(DAW[3]), ._4O(DAW[4]), ._5O(DAW[5]), ._6O(DAW[6]), ._7O(DAW[7]));
  _74LS541 _74ls541_2 (
    .nOE1(not_20_out), .nOE2(not_20_out), ._0D(ACC[8]), ._1D(ACC[9]), ._2D(ACC[10]), ._3D(ACC[11]),
    ._4D(1'b0), ._5D(1'b0), ._6D(1'b0), ._7D(1'b0), ._0O(DAW[8]), ._1O(DAW[9]), ._2O(DAW[10]), ._3O(DAW[11]));  // open: _4O, _5O, _6O, _7O
  _74LS541 _74ls541_3 (
    .nOE1(not_21_out), .nOE2(not_21_out), ._0D(ACC[0]), ._1D(ACC[1]), ._2D(ACC[2]), ._3D(ACC[3]),
    ._4D(ACC[4]), ._5D(ACC[5]), ._6D(ACC[6]), ._7D(ACC[7]), ._0O(ABUS[0]), ._1O(ABUS[1]), ._2O(ABUS[2]),
    ._3O(ABUS[3]), ._4O(ABUS[4]), ._5O(ABUS[5]), ._6O(ABUS[6]), ._7O(ABUS[7]));
  _74LS541 _74ls541_4 (
    .nOE1(not_21_out), .nOE2(not_21_out), ._0D(ACC[8]), ._1D(ACC[9]), ._2D(ACC[10]), ._3D(ACC[11]),
    ._4D(1'b0), ._5D(1'b0), ._6D(1'b0), ._7D(1'b0), ._0O(ABUS[8]), ._1O(ABUS[9]), ._2O(ABUS[10]),
    ._3O(ABUS[11]));  // open: _4O, _5O, _6O, _7O
  _74LS273 _74ls273_3 (
    .CP(or_28_out), .nMR(1'b1), .D0(PC[0]), .D1(PC[1]), .D2(PC[2]), .D3(PC[3]), .D4(PC[4]), .D5(PC[5]),
    .D6(PC[6]), .D7(PC[7]), .Q0(IRA[0]), .Q1(IRA[1]), .Q2(IRA[2]), .Q3(IRA[3]), .Q4(IRA[4]), .Q5(IRA[5]),
    .Q6(IRA[6]), .Q7(IRA[7]));
  _74LS273 _74ls273_4 (
    .CP(or_28_out), .nMR(1'b1), .D0(PC[8]), .D1(PC[9]), .D2(PC[10]), .D3(PC[11]), .D4(1'b0), .D5(1'b0),
    .D6(1'b0), .D7(1'b0), .Q0(IRA[8]), .Q1(IRA[9]), .Q2(IRA[10]), .Q3(IRA[11]));  // open: Q4, Q5, Q6, Q7
  _74LS273 _74ls273_5 (
    .CP(or_28_out), .nMR(1'b1), .D0(DAW[0]), .D1(DAW[1]), .D2(DAW[2]), .D3(DAW[3]), .D4(DAW[4]), .D5(DAW[5]),
    .D6(DAW[6]), .D7(DAW[7]), .Q0(IR[0]), .Q1(IR[1]), .Q2(IR[2]), .Q3(IR[3]), .Q4(IR[4]), .Q5(IR[5]),
    .Q6(IR[6]), .Q7(IR[7]));
  _74LS273 _74ls273_6 (
    .CP(or_28_out), .nMR(1'b1), .D0(DAW[8]), .D1(DAW[9]), .D2(DAW[10]), .D3(DAW[11]), .D4(1'b0), .D5(1'b0),
    .D6(1'b0), .D7(1'b0), .Q0(IR[8]), .Q1(IR[9]), .Q2(IR[10]), .Q3(IR[11]));  // open: Q4, Q5, Q6, Q7
  Comparator #(.Bits(12)) comparator_1 (.a(in_4), .b(IRA), .eq(comparator_1_eq));  // open: gt, lt
  // Probe on ACC
  // Probe on DAW[11:0]
  LED led_7 (.in(L1));
  // Probe on ABUS
  LED led_8 (.in(enACCtoABUS));
  and and_7 (BP, comparator_1_eq, in_5, or_28_out);
  Seven_Seg_Hex seven_seg_hex_5 (.d({1'b0, IRA[11:9]}), .dp(1'b0));
  // Probe on BP
  Seven_Seg_Hex seven_seg_hex_6 (.d({1'b0, IRA[8:6]}), .dp(1'b0));
  LED led_9 (.in(L_GEN[10]));
  LED led_10 (.in(AND));
  LED led_11 (.in(L_OPR3[12]));
  LED led_12 (.in(L_OPR3[11]));
  LED led_13 (.in(L_OPR2[8]));
  LED led_14 (.in(CLA_2));
  LED led_15 (.in(CLA_1));
  LED led_16 (.in(L_OPR1[10]));
  Seven_Seg_Hex seven_seg_hex_7 (.d({1'b0, IRA[5:3]}), .dp(1'b0));
  nor nor_1 (nor_1_out, CLA_4, pulldown_14_out);
  PullDown pulldown_14 (.out(pulldown_14_out));
  LED led_17 (.in(ISZ));
  LED led_18 (.in(L_OPR3[10]));
  LED led_19 (.in(L_OPR2[7]));
  LED led_20 (.in(CLL));
  Button R (.out(R_out));
  or or_29 (or_29_out, H_out, STOPSOON);
  Button H (.out(H_out));
  Button S (.out(S_out));
  Button T (.out(T_out));
  and and_8 (and_8_out, T_out, _25Hz);
  Seven_Seg_Hex seven_seg_hex_8 (.d({1'b0, IRA[2:0]}), .dp(1'b0));
  ROM #(.AddrBits(12), .Bits(51)) CharRom3x (
    .A(IR), .sel(1'b1),
    .D({CharRom3x_d_4[50], fIndirect, isCurrPage, CharRom3x_d_3, CharRom3x_d_2, CharRom3x_d}));
  // Probe on iDone
  RAMSPY ramspy_1 (.Trig({12{1'b0}}), .DAW({DAW[24], ABUS, DAW[11:0]}), .O(ramspy_1_o));
  RAMSPY ramspy_2 (.Trig(12'h2), .DAW({DAW[24], ABUS, DAW[11:0]}), .O(ramspy_2_o));
  LED led_21 (.in(CODE_lsb));
  // Probe on CODE_lsb
  PullDown pulldown_15 (.out(enMQclear));
  not not_22 (not_22_out, enMQclear);
  // Probe on ACC
  or or_30 (or_30_out, ckMQ_1, ckACC_5);
  or or_31 (L9, enACCtoDBUS_2, CLA_4);
  LED led_22 (.in(DCA));
  LED led_23 (.in(L_OPR3[9]));
  LED led_24 (.in(L_OPR2[6]));
  LED led_25 (.in(CMA));
  OneShot oneshot_2 (.i(R_out), .o(oneshot_2_o));
  OneShot oneshot_3 (.i(or_29_out), .o(oneshot_3_o));
  or or_32 (or_32_out, S_out, and_8_out);
  // Probe on ramspy_1_o
  // Probe on ramspy_2_o
  LED led_26 (.in(CODE_mid));
  LED led_27 (.in(CODE_msb));
  // Probe on CODE_mid
  // Probe on CODE_msb
  LED led_28 (.in(JMS));
  LED led_29 (.in(JMP));
  LED led_30 (.in(L_OPR3[8]));
  LED led_31 (.in(L_OPR3[7]));
  LED led_32 (.in(L_OPR2[4]));
  LED led_33 (.in(L_OPR2[5]));
  LED led_34 (.in(CML));
  LED led_35 (.in(IAC));
  or or_33 (or_33_out, oneshot_3_o, BP);
  OneShot oneshot_4 (.i(or_32_out), .o(oneshot_4_o));
  LED led_36 (.in(fGIE));
  LED led_37 (.in(L_CPU[7]));
  LED led_38 (.in(L_PRN[5]));
  LED led_39 (.in(KCF_6030));
  Seven_Seg_Hex seven_seg_hex_9 (.d({1'b0, IR[11:9]}), .dp(1'b0));
  SixteenSeg sixteenseg_1 (.led(CharRom3x_d), .dp(CharRom3x_d_4[50]));
  LED led_40 (.in(MQL));
  // Probe on MQL
  _74LS273 _74ls273_7 (
    .CP(or_30_out), .nMR(not_22_out), .D0(ACC[0]), .D1(ACC[1]), .D2(ACC[2]), .D3(ACC[3]), .D4(ACC[4]),
    .D5(ACC[5]), .D6(ACC[6]), .D7(ACC[7]), .Q0(_74ls273_7_q0), .Q1(_74ls273_7_q1), .Q2(_74ls273_7_q2),
    .Q3(_74ls273_7_q3), .Q4(_74ls273_7_q4), .Q5(_74ls273_7_q5), .Q6(_74ls273_7_q6), .Q7(_74ls273_7_q7));
  _74LS273 _74ls273_8 (
    .CP(or_30_out), .nMR(not_22_out), .D0(ACC[8]), .D1(ACC[9]), .D2(ACC[10]), .D3(ACC[11]), .D4(1'b0),
    .D5(1'b0), .D6(1'b0), .D7(1'b0), .Q0(_74ls273_8_q0), .Q1(_74ls273_8_q1), .Q2(_74ls273_8_q2),
    .Q3(_74ls273_8_q3));  // open: Q4, Q5, Q6, Q7
  LED led_41 (.in(IOT));
  LED led_42 (.in(L_OPR3[6]));
  LED led_43 (.in(L_OPR2[3]));
  LED led_44 (.in(L_OPR1[4]));
  RS_FF_AS rs_ff_as_1 (.S(oneshot_2_o), .R(or_33_out), .Q(rs_ff_as_1_q), .nQ(rs_ff_as_1_nq));
  LED led_45 (.in(L_IRQ[5]));
  LED led_46 (.in(ION_6001));
  LED led_47 (.in(L_PRN[4]));
  LED led_48 (.in(KSF_6031));
  Seven_Seg_Hex seven_seg_hex_10 (.d({1'b0, IR[8:6]}), .dp(1'b0));
  SixteenSeg sixteenseg_2 (.led(CharRom3x_d_2), .dp(CharRom3x_d_4[50]));
  LED CURRENT_PAGE (.in(isCurrPage));
  LED u_INDIRECT (.in(fIndirect));
  not not_23 (not_23_out, IR[4]);
  not not_24 (not_24_out, IR[5]);
  not not_25 (not_25_out, IR[6]);
  not not_26 (not_26_out, isCurrPage);
  RAMSPY ramspy_3 (.Trig(12'h7e7), .DAW({DAW[24], ABUS, DAW[11:0]}), .O(ramspy_3_o));
  LED led_49 (.in(SCA));
  // Probe on SCA
  not not_27 (not_27_out, L9);
  LED led_50 (.in(L_GEN[4]));
  LED led_51 (.in(L_OPR3[5]));
  LED led_52 (.in(L_OPR2[2]));
  LED led_53 (.in(L_OPR1[3]));
  PullDown pulldown_16 (.out(L_GEN[3]));
  OneShot oneshot_5 (.i(rs_ff_as_1_q), .o(oneshot_5_o));
  RS_FF_AS rs_ff_as_2 (.S(oneshot_4_o), .R(iDone), .Q(rs_ff_as_2_q));  // open: nQ
  LED led_54 (.in(fIrqDly));
  LED led_55 (.in(enIRQ));
  LED led_56 (.in(IOF_6002));
  LED led_57 (.in(L_CPU[4]));
  LED led_58 (.in(L_PRN[3]));
  LED led_59 (.in(L_PRN[2]));
  LED led_60 (.in(KCC_6032));
  LED led_61 (.in(KRS_6034));
  Seven_Seg_Hex seven_seg_hex_11 (.d({1'b0, IR[5:3]}), .dp(1'b0));
  SixteenSeg sixteenseg_3 (.led(CharRom3x_d_3), .dp(CharRom3x_d_4[50]));
  and and_9 (fAutoinc, fIndirect, IR[3], not_23_out, not_24_out, not_25_out, not_26_out);
  LED led_62 (.in(MQA));
  LED led_63 (.in(CLA_3));
  // Probe on MQA
  // Probe on CLA_3
  _74LS373 _74ls373_1 (
    .Q0(MQ[0]), .Q1(MQ[1]), .Q2(MQ[2]), .Q3(MQ[3]), .Q4(MQ[4]), .Q5(MQ[5]), .Q6(MQ[6]), .Q7(MQ[7]),
    .nOC(1'b0), .C(nor_1_out), .D0(_74ls273_7_q0), .D1(_74ls273_7_q1), .D2(_74ls273_7_q2),
    .D3(_74ls273_7_q3), .D4(_74ls273_7_q4), .D5(_74ls273_7_q5), .D6(_74ls273_7_q6), .D7(_74ls273_7_q7));
  _74LS373 _74ls373_2 (
    .Q0(MQ[8]), .Q1(MQ[9]), .Q2(MQ[10]), .Q3(MQ[11]), .nOC(1'b0), .C(nor_1_out), .D0(_74ls273_8_q0),
    .D1(_74ls273_8_q1), .D2(_74ls273_8_q2), .D3(_74ls273_8_q3), .D4(1'b0), .D5(1'b0), .D6(1'b0), .D7(1'b0));  // open: Q4, Q5, Q6, Q7
  LED led_64 (.in(L_GEN[3]));
  LED led_65 (.in(fIndirect));
  LED led_66 (.in(L_OPR3[4]));
  LED led_67 (.in(L_OPR3[3]));
  LED led_68 (.in(L_OPR2[1]));
  LED led_69 (.in(HLT));
  LED led_70 (.in(L_OPR1[2]));
  LED led_71 (.in(L_OPR1[1]));
  or or_34 (or_34_out, oneshot_5_o, oneshot_4_o);
  or or_35 (or_35_out, rs_ff_as_1_nq, rs_ff_as_2_q);
  LED led_72 (.in(L_IRQ[2]));
  LED led_73 (.in(GTF_6004));
  LED led_74 (.in(L_PRN[1]));
  LED led_75 (.in(KIE_6035));
  Seven_Seg_Hex seven_seg_hex_12 (.d({1'b0, IR[2:0]}), .dp(1'b0));
  Seven_Seg_Hex seven_seg_hex_13 (.d({3'b000, IR[6]}), .dp(1'b0));
  // Probe on ramspy_3_o
  LED led_76 (.in(fAutoinc));
  LED led_77 (.in(L_OPR3[2]));
  LED led_78 (.in(BSW));
  PullDown pulldown_17 (.out(L_OPR1[10]));
  and and_10 (and_10_out, or_35_out, iDone);
  D_FF d_ff_2 (.D(1'b1), .C(_25Hz), .Q(d_ff_2_q));  // open: nQ
  LED led_79 (.in(fKBD));
  LED led_80 (.in(L_CPU[2]));
  LED led_81 (.in(L_PRN[0]));
  LED led_82 (.in(KRB_6036));
  Seven_Seg_Hex seven_seg_hex_14 (.d({1'b0, IR[5:3]}), .dp(1'b0));
  LED led_83 (.in(isCurrPage));
  LED led_84 (.in(L_OPR3[1]));
  OneShot oneshot_6 (.i(and_10_out), .o(oneshot_6_o));
  D_FF d_ff_3 (.D(d_ff_2_q), .C(_25Hz), .nQ(d_ff_3_nq));  // open: Q
  LED led_85 (.in(fPRN));
  LED led_86 (.in(L_CPU[1]));
  LED led_87 (.in(CAF_6007));
  Seven_Seg_Hex seven_seg_hex_15 (.d({1'b0, IR[2:0]}), .dp(1'b0));
  LED led_88 (.in(L_OPR3[0]));
  RS_FF_AS rs_ff_as_3 (.S(or_34_out), .R(oneshot_6_o), .Q(rs_ff_as_3_q));  // open: nQ
  and and_11 (and_11_out, d_ff_2_q, d_ff_3_nq);
  LED led_89 (.in(MOP1));
  // Probe on MOP1
  LED led_90 (.in(MOP2));
  // Probe on MOP2
  LED led_91 (.in(MOP3));
  // Probe on MOP3
  LED led_92 (.in(rs_ff_as_3_q));
  Seven_Seg_Hex seven_seg_hex_16 (.d({1'b0, ABUS[11:9]}), .dp(1'b0));
  Seven_Seg_Hex seven_seg_hex_17 (.d({1'b0, DAW[11:9]}), .dp(1'b0));
  Seven_Seg_Hex seven_seg_hex_18 (.d({1'b0, ACC[11:9]}), .dp(1'b0));
  LED led_93 (.in(LINK));
  Seven_Seg_Hex seven_seg_hex_19 (.d({1'b0, MQ[11:9]}), .dp(1'b0));
  _74LS541 _74ls541_5 (
    .nOE1(not_27_out), .nOE2(not_27_out), ._0D(MQ[0]), ._1D(MQ[1]), ._2D(MQ[2]), ._3D(MQ[3]), ._4D(MQ[4]),
    ._5D(MQ[5]), ._6D(MQ[6]), ._7D(MQ[7]), ._0O(OBUS[0]), ._1O(OBUS[1]), ._2O(OBUS[2]), ._3O(OBUS[3]),
    ._4O(OBUS[4]), ._5O(OBUS[5]), ._6O(OBUS[6]), ._7O(OBUS[7]));
  _74LS541 _74ls541_6 (
    .nOE1(not_27_out), .nOE2(not_27_out), ._0D(MQ[8]), ._1D(MQ[9]), ._2D(MQ[10]), ._3D(MQ[11]), ._4D(1'b0),
    ._5D(1'b0), ._6D(1'b0), ._7D(1'b0), ._0O(OBUS[8]), ._1O(OBUS[9]), ._2O(OBUS[10]), ._3O(OBUS[11]));  // open: _4O, _5O, _6O, _7O
  LED led_94 (.in(fGIE));
  LED led_95 (.in(L_IRQ[5]));
  LED led_96 (.in(L_CPU[7]));
  LED led_97 (.in(ION_6001));
  LED led_98 (.in(KCF_6030));
  LED led_99 (.in(KSF_6031));
  LED led_100 (.in(L_PRN[4]));
  LED led_101 (.in(L_PRN[5]));
  and and_12 (and_12_out, rs_ff_as_3_q, MAX);
  or or_36 (ckSetPC_0, and_11_out, _2_out);
  Button _2 (.out(_2_out));
  Seven_Seg_Hex seven_seg_hex_20 (.d({1'b0, ABUS[8:6]}), .dp(1'b0));
  Seven_Seg_Hex seven_seg_hex_21 (.d({1'b0, DAW[8:6]}), .dp(1'b0));
  Seven_Seg_Hex seven_seg_hex_22 (.d({1'b0, ACC[8:6]}), .dp(1'b0));
  Seven_Seg_Hex seven_seg_hex_23 (.d({1'b0, MQ[8:6]}), .dp(1'b0));
  LED led_102 (.in(fIrqDly));
  LED led_103 (.in(IOF_6002));
  LED led_104 (.in(KCC_6032));
  LED led_105 (.in(L_PRN[3]));
  Button M (.out(M_out));
  or or_37 (CLK_t, M_out, and_12_out);
  Delay #(.delayTime(5)) delay_1 (.in(ckSetPC_0), .out(enPCtoABUS_0));
  Delay #(.delayTime(10)) delay_2 (.in(ckSetPC_0), .out(ckIR_0));
  Seven_Seg_Hex seven_seg_hex_24 (.d({1'b0, ABUS[5:3]}), .dp(1'b0));
  Seven_Seg_Hex seven_seg_hex_25 (.d({1'b0, DAW[5:3]}), .dp(1'b0));
  Seven_Seg_Hex seven_seg_hex_26 (.d({1'b0, ACC[5:3]}), .dp(1'b0));
  Seven_Seg_Hex seven_seg_hex_27 (.d({1'b0, MQ[5:3]}), .dp(1'b0));
  LED led_106 (.in(enIRQ));
  LED led_107 (.in(L_CPU[4]));
  LED led_108 (.in(KRS_6034));
  LED led_109 (.in(L_PRN[2]));
  Seven_Seg_Hex seven_seg_hex_28 (.d({1'b0, ABUS[2:0]}), .dp(1'b0));
  Seven_Seg_Hex seven_seg_hex_29 (.d({1'b0, DAW[2:0]}), .dp(1'b0));
  Seven_Seg_Hex seven_seg_hex_30 (.d({1'b0, ACC[2:0]}), .dp(1'b0));
  Seven_Seg_Hex seven_seg_hex_31 (.d({1'b0, MQ[2:0]}), .dp(1'b0));
  // Probe on OBUS
  LED led_110 (.in(L9));
  LED led_111 (.in(L_IRQ[2]));
  LED led_112 (.in(fKBD));
  LED led_113 (.in(GTF_6004));
  LED led_114 (.in(L_CPU[2]));
  LED led_115 (.in(KIE_6035));
  LED led_116 (.in(KRB_6036));
  LED led_117 (.in(L_PRN[1]));
  LED led_118 (.in(L_PRN[0]));
  LED led_119 (.in(fPRN));
  LED led_120 (.in(L_CPU[1]));
  LED led_121 (.in(CAF_6007));
  PullUp #(.Bits(13)) pullup_2 (.out(L_OPR3));
  PullUp #(.Bits(12)) pullup_3 (.out({AND, L_GEN[10], ISZ, DCA, JMS, JMP, IOT, L_GEN[4:3], fIndirect, fAutoinc, isCurrPage}));
  nor nor_2 (nor_2_out, CLA_1, CLA_2, CLA_3, CLA_4);
  not not_28 (not_28_out, enALUand);
  PullUp #(.Bits(6)) pullup_4 (.out(L_PRN));
  PullUp #(.Bits(6)) pullup_5 (.out({KCF_6030, KSF_6031, KCC_6032, KRS_6034, KIE_6035, KRB_6036}));
  PullUp #(.Bits(8)) pullup_6 (.out({L_CPU[7], ION_6001, IOF_6002, L_CPU[4], GTF_6004, L_CPU[2:1], CAF_6007}));
  or or_38 (or_38_out, enALUor_mop2, enACCtoDBUS_2, CLA_4);
  or or_39 (or_39_out, DAW[0], not_28_out);
  or or_40 (or_40_out, DAW[1], not_28_out);
  or or_41 (or_41_out, DAW[2], not_28_out);
  or or_42 (or_42_out, DAW[3], not_28_out);
  or or_43 (or_43_out, DAW[4], not_28_out);
  or or_44 (or_44_out, DAW[5], not_28_out);
  or or_45 (or_45_out, DAW[6], not_28_out);
  or or_46 (or_46_out, DAW[7], not_28_out);
  or or_47 (or_47_out, DAW[8], not_28_out);
  or or_48 (or_48_out, DAW[9], not_28_out);
  or or_49 (or_49_out, DAW[10], not_28_out);
  or or_50 (or_50_out, DAW[11], not_28_out);
  not not_29 (CLA, nor_2_out);
  and and_13 (and_13_out[0], DAW[0], enALUadd);
  and and_14 (and_13_out[1], DAW[1], enALUadd);
  and and_15 (and_13_out[2], DAW[2], enALUadd);
  and and_16 (and_13_out[3], DAW[3], enALUadd);
  and and_17 (and_17_out[0], DAW[4], enALUadd);
  and and_18 (and_17_out[1], DAW[5], enALUadd);
  and and_19 (and_17_out[2], DAW[6], enALUadd);
  and and_20 (and_17_out[3], DAW[7], enALUadd);
  and and_21 (and_21_out[0], DAW[8], enALUadd);
  and and_22 (and_21_out[1], DAW[9], enALUadd);
  and and_23 (and_21_out[2], DAW[10], enALUadd);
  and and_24 (and_21_out[3], DAW[11], enALUadd);
  or or_51 (or_51_out, enALUtoACC_mop1, enALUtoACC_andtad, enALUtoACC_mop2, enACCtoDBUS_2, CLA_4);
  and and_25 (and_25_out, ACC[0], or_39_out, nor_2_out);
  and and_26 (and_26_out, ACC[1], or_40_out, nor_2_out);
  and and_27 (and_27_out, ACC[2], or_41_out, nor_2_out);
  and and_28 (and_28_out, ACC[3], or_42_out, nor_2_out);
  and and_29 (and_29_out, ACC[4], or_43_out, nor_2_out);
  and and_30 (and_30_out, ACC[5], or_44_out, nor_2_out);
  and and_31 (and_31_out, ACC[6], or_45_out, nor_2_out);
  and and_32 (and_32_out, ACC[7], or_46_out, nor_2_out);
  and and_33 (and_33_out, ACC[8], or_47_out, nor_2_out);
  and and_34 (and_34_out, ACC[9], or_48_out, nor_2_out);
  and and_35 (and_35_out, ACC[10], or_49_out, nor_2_out);
  and and_36 (and_36_out, ACC[11], or_50_out, nor_2_out);
  Seven_Seg_Hex seven_seg_hex_32 (.d({1'b0, OBUS[11:9]}), .dp(1'b0));
  and and_37 (and_48_out[0], OBUS[0], or_38_out);
  Seven_Seg_Hex seven_seg_hex_33 (.d({1'b0, OBUS[8:6]}), .dp(1'b0));
  and and_38 (and_48_out[1], OBUS[1], or_38_out);
  or or_52 (or_52_out, and_25_out, and_48_out[0]);
  or or_53 (or_53_out, and_26_out, and_48_out[1]);
  or or_54 (or_54_out, and_27_out, and_48_out[2]);
  or or_55 (or_55_out, and_28_out, and_48_out[3]);
  or or_56 (or_56_out, and_29_out, and_48_out[4]);
  or or_57 (or_57_out, and_30_out, and_48_out[5]);
  or or_58 (or_58_out, and_31_out, and_48_out[6]);
  or or_59 (or_59_out, and_32_out, and_48_out[7]);
  or or_60 (or_60_out, and_33_out, and_48_out[8]);
  or or_61 (or_61_out, and_34_out, and_48_out[9]);
  or or_62 (or_62_out, and_35_out, and_48_out[10]);
  or or_63 (or_63_out, and_36_out, and_48_out[11]);
  Seven_Seg_Hex seven_seg_hex_34 (.d({1'b0, OBUS[5:3]}), .dp(1'b0));
  and and_39 (and_48_out[3], OBUS[3], or_38_out);
  and and_40 (and_48_out[2], OBUS[2], or_38_out);
  Seven_Seg_Hex seven_seg_hex_35 (.d({1'b0, OBUS[2:0]}), .dp(1'b0));
  and and_41 (and_48_out[4], OBUS[4], or_38_out);
  xor xor_3 (xor_3_out, CMA, or_52_out);
  xor xor_4 (xor_4_out, CMA, or_53_out);
  xor xor_5 (xor_5_out, CMA, or_54_out);
  xor xor_6 (xor_6_out, CMA, or_55_out);
  xor xor_7 (xor_7_out, CMA, or_56_out);
  xor xor_8 (xor_8_out, CMA, or_57_out);
  xor xor_9 (xor_9_out, CMA, or_58_out);
  xor xor_10 (xor_10_out, CMA, or_59_out);
  xor xor_11 (xor_11_out, CMA, or_60_out);
  xor xor_12 (xor_12_out, CMA, or_61_out);
  xor xor_13 (xor_13_out, CMA, or_62_out);
  xor xor_14 (xor_14_out, CMA, or_63_out);
  and and_42 (and_48_out[5], OBUS[5], or_38_out);
  and and_43 (and_48_out[7], OBUS[7], or_38_out);
  and and_44 (and_48_out[6], OBUS[6], or_38_out);
  nand nand_1 (nand_1_out, BSW, or_51_out);
  nand nand_2 (nand_2_out, L_OPR1[1], or_51_out);
  nand nand_3 (nand_3_out, L_OPR1[2], or_51_out);
  nand nand_4 (nand_4_out, L_OPR1[4], or_51_out);
  nand nand_5 (nand_5_out, L_OPR1[3], or_51_out);
  and and_45 (and_48_out[8], OBUS[8], or_38_out);
  _74LS283 _74ls283_4 (
    .A1(and_13_out[0]), .A2(and_13_out[1]), .A3(and_13_out[2]), .A4(and_13_out[3]), .B1(xor_3_out),
    .B2(xor_4_out), .B3(xor_5_out), .B4(xor_6_out), .S1(_74ls283_4_s1), .S2(_74ls283_4_s2),
    .S3(_74ls283_4_s3), .S4(_74ls283_4_s4), .C_in(IAC), .C_out(_74ls283_4_c_out));
  _74LS283 _74ls283_5 (
    .A1(and_17_out[0]), .A2(and_17_out[1]), .A3(and_17_out[2]), .A4(and_17_out[3]), .B1(xor_7_out),
    .B2(xor_8_out), .B3(xor_9_out), .B4(xor_10_out), .S1(_74ls283_5_s1), .S2(_74ls283_5_s2),
    .S3(_74ls283_5_s3), .S4(_74ls283_5_s4), .C_in(_74ls283_4_c_out), .C_out(_74ls283_5_c_out));
  _74LS283 _74ls283_6 (
    .A1(and_21_out[0]), .A2(and_21_out[1]), .A3(and_21_out[2]), .A4(and_21_out[3]), .B1(xor_11_out),
    .B2(xor_12_out), .B3(xor_13_out), .B4(xor_14_out), .S1(_74ls283_6_s1), .S2(_74ls283_6_s2),
    .S3(_74ls283_6_s3), .S4(_74ls283_6_s4), .C_in(_74ls283_5_c_out), .C_out(IAC_carryout));
  nand nand_6 (nand_6_out, or_51_out, and_46_out);
  and and_46 (and_46_out, nand_1_out, nand_2_out, nand_3_out, nand_4_out, nand_5_out);
  and and_47 (and_48_out[9], OBUS[9], or_38_out);
  and and_48 (and_48_out[11], OBUS[11], or_38_out);
  and and_49 (and_48_out[10], OBUS[10], or_38_out);
  _74LS541 _74ls541_7 (
    .nOE1(nand_6_out), .nOE2(nand_6_out), ._0D(_74ls283_4_s1), ._1D(_74ls283_4_s2), ._2D(_74ls283_4_s3),
    ._3D(_74ls283_4_s4), ._4D(_74ls283_5_s1), ._5D(_74ls283_5_s2), ._6D(_74ls283_5_s3), ._7D(_74ls283_5_s4),
    ._0O(ALU_out[0]), ._1O(ALU_out[1]), ._2O(ALU_out[2]), ._3O(ALU_out[3]), ._4O(ALU_out[4]),
    ._5O(ALU_out[5]), ._6O(ALU_out[6]), ._7O(ALU_out[7]));
  _74LS541 _74ls541_8 (
    .nOE1(nand_6_out), .nOE2(nand_6_out), ._0D(_74ls283_6_s1), ._1D(_74ls283_6_s2), ._2D(_74ls283_6_s3),
    ._3D(_74ls283_6_s4), ._4D(1'b0), ._5D(1'b0), ._6D(1'b0), ._7D(ALU_Lin), ._0O(ALU_out[8]),
    ._1O(ALU_out[9]), ._2O(ALU_out[10]), ._3O(ALU_out[11]), ._7O(ALU_Lout));  // open: _4O, _5O, _6O
  _74LS541 _74ls541_9 (
    .nOE1(nand_1_out), .nOE2(nand_1_out), ._0D(_74ls283_5_s3), ._1D(_74ls283_5_s4), ._2D(_74ls283_6_s1),
    ._3D(_74ls283_6_s2), ._4D(_74ls283_6_s3), ._5D(_74ls283_6_s4), ._6D(_74ls283_4_s1), ._7D(_74ls283_4_s2),
    ._0O(ALU_out[0]), ._1O(ALU_out[1]), ._2O(ALU_out[2]), ._3O(ALU_out[3]), ._4O(ALU_out[4]),
    ._5O(ALU_out[5]), ._6O(ALU_out[6]), ._7O(ALU_out[7]));
  _74LS541 _74ls541_10 (
    .nOE1(nand_1_out), .nOE2(nand_1_out), ._0D(_74ls283_4_s3), ._1D(_74ls283_4_s4), ._2D(_74ls283_5_s1),
    ._3D(_74ls283_5_s2), ._4D(1'b0), ._5D(1'b0), ._6D(1'b0), ._7D(ALU_Lin), ._0O(ALU_out[8]),
    ._1O(ALU_out[9]), ._2O(ALU_out[10]), ._3O(ALU_out[11]), ._7O(ALU_Lout));  // open: _4O, _5O, _6O
  _74LS541 _74ls541_11 (
    .nOE1(nand_2_out), .nOE2(nand_2_out), ._0D(ALU_Lin), ._1D(_74ls283_4_s1), ._2D(_74ls283_4_s2),
    ._3D(_74ls283_4_s3), ._4D(_74ls283_4_s4), ._5D(_74ls283_5_s1), ._6D(_74ls283_5_s2), ._7D(_74ls283_5_s3),
    ._0O(ALU_out[0]), ._1O(ALU_out[1]), ._2O(ALU_out[2]), ._3O(ALU_out[3]), ._4O(ALU_out[4]),
    ._5O(ALU_out[5]), ._6O(ALU_out[6]), ._7O(ALU_out[7]));
  _74LS541 _74ls541_12 (
    .nOE1(nand_2_out), .nOE2(nand_2_out), ._0D(_74ls283_5_s4), ._1D(_74ls283_6_s1), ._2D(_74ls283_6_s2),
    ._3D(_74ls283_6_s3), ._4D(1'b0), ._5D(1'b0), ._6D(1'b0), ._7D(_74ls283_6_s4), ._0O(ALU_out[8]),
    ._1O(ALU_out[9]), ._2O(ALU_out[10]), ._3O(ALU_out[11]), ._7O(ALU_Lout));  // open: _4O, _5O, _6O
  _74LS541 _74ls541_13 (
    .nOE1(nand_3_out), .nOE2(nand_3_out), ._0D(_74ls283_6_s4), ._1D(ALU_Lin), ._2D(_74ls283_4_s1),
    ._3D(_74ls283_4_s2), ._4D(_74ls283_4_s3), ._5D(_74ls283_4_s4), ._6D(_74ls283_5_s1), ._7D(_74ls283_5_s2),
    ._0O(ALU_out[0]), ._1O(ALU_out[1]), ._2O(ALU_out[2]), ._3O(ALU_out[3]), ._4O(ALU_out[4]),
    ._5O(ALU_out[5]), ._6O(ALU_out[6]), ._7O(ALU_out[7]));
  _74LS541 _74ls541_14 (
    .nOE1(nand_3_out), .nOE2(nand_3_out), ._0D(_74ls283_5_s3), ._1D(_74ls283_5_s4), ._2D(_74ls283_6_s1),
    ._3D(_74ls283_6_s2), ._4D(1'b0), ._5D(1'b0), ._6D(1'b0), ._7D(_74ls283_6_s3), ._0O(ALU_out[8]),
    ._1O(ALU_out[9]), ._2O(ALU_out[10]), ._3O(ALU_out[11]), ._7O(ALU_Lout));  // open: _4O, _5O, _6O
  _74LS541 _74ls541_15 (
    .nOE1(nand_4_out), .nOE2(nand_4_out), ._0D(_74ls283_4_s2), ._1D(_74ls283_4_s3), ._2D(_74ls283_4_s4),
    ._3D(_74ls283_5_s1), ._4D(_74ls283_5_s2), ._5D(_74ls283_5_s3), ._6D(_74ls283_5_s4), ._7D(_74ls283_6_s1),
    ._0O(ALU_out[0]), ._1O(ALU_out[1]), ._2O(ALU_out[2]), ._3O(ALU_out[3]), ._4O(ALU_out[4]),
    ._5O(ALU_out[5]), ._6O(ALU_out[6]), ._7O(ALU_out[7]));
  _74LS541 _74ls541_16 (
    .nOE1(nand_4_out), .nOE2(nand_4_out), ._0D(_74ls283_6_s2), ._1D(_74ls283_6_s3), ._2D(_74ls283_6_s4),
    ._3D(ALU_Lin), ._4D(1'b0), ._5D(1'b0), ._6D(1'b0), ._7D(_74ls283_4_s1), ._0O(ALU_out[8]),
    ._1O(ALU_out[9]), ._2O(ALU_out[10]), ._3O(ALU_out[11]), ._7O(ALU_Lout));  // open: _4O, _5O, _6O
  _74LS541 _74ls541_17 (
    .nOE1(nand_5_out), .nOE2(nand_5_out), ._0D(_74ls283_4_s3), ._1D(_74ls283_4_s4), ._2D(_74ls283_5_s1),
    ._3D(_74ls283_5_s2), ._4D(_74ls283_5_s3), ._5D(_74ls283_5_s4), ._6D(_74ls283_6_s1), ._7D(_74ls283_6_s2),
    ._0O(ALU_out[0]), ._1O(ALU_out[1]), ._2O(ALU_out[2]), ._3O(ALU_out[3]), ._4O(ALU_out[4]),
    ._5O(ALU_out[5]), ._6O(ALU_out[6]), ._7O(ALU_out[7]));
  _74LS541 _74ls541_18 (
    .nOE1(nand_5_out), .nOE2(nand_5_out), ._0D(_74ls283_6_s3), ._1D(_74ls283_6_s4), ._2D(ALU_Lin),
    ._3D(_74ls283_4_s1), ._4D(1'b0), ._5D(1'b0), ._6D(1'b0), ._7D(_74ls283_4_s2), ._0O(ALU_out[8]),
    ._1O(ALU_out[9]), ._2O(ALU_out[10]), ._3O(ALU_out[11]), ._7O(ALU_Lout));  // open: _4O, _5O, _6O
  or or_64 (or_64_out, AND, L_GEN[10]);
  or or_65 (or_65_out, AND, L_GEN[10], DCA, JMP, JMS);
  and and_50 (and_50_out, aiFinished, or_64_out);
  and and_51 (and_51_out, aiFinished, DCA);
  and and_52 (and_52_out, aiFinished, JMP);
  and and_53 (and_53_out, aiFinished, JMS);
  _74LS238 _74ls238_1 (
    .A(IR[9]), .B(IR[10]), .C(IR[11]), .G(1'b1), .nGB(1'b0), .nGA(inhibitIR), .Y0(AND), .Y1(L_GEN[10]),
    .Y2(ISZ), .Y3(DCA), .Y4(JMS), .Y5(JMP), .Y6(IOT), .Y7(L_GEN[4]));
  not not_30 (not_30_out, IR[0]);
  not not_31 (not_31_out, IR[8]);
  _74LS238 _74ls238_2 (
    .A(IR[3]), .B(IR[4]), .C(IR[5]), .G(IOT), .nGB(1'b0), .nGA(1'b0), .Y0(IOT_CPU), .Y1(IOT_HISPEEDREADER),
    .Y2(IOT_HISPEEDPUNCH), .Y3(IOT_TTYREADER), .Y4(IOT_TTYPUNCH));  // open: Y5, Y6, Y7
  _74LS238 _74ls238_3 (
    .A(IR[0]), .B(IR[1]), .C(IR[2]), .G(IOT_CPU), .nGB(1'b0), .nGA(1'b0), .Y0(L_CPU[7]), .Y1(ION_6001),
    .Y2(IOF_6002), .Y3(L_CPU[4]), .Y4(GTF_6004), .Y5(L_CPU[2]), .Y6(L_CPU[1]), .Y7(CAF_6007));
  _74LS238 _74ls238_4 (
    .A(IR[0]), .B(IR[1]), .C(IR[2]), .G(IOT_TTYREADER), .nGB(1'b0), .nGA(1'b0), .Y0(KCF_6030), .Y1(KSF_6031),
    .Y2(KCC_6032), .Y4(KRS_6034), .Y5(KIE_6035), .Y6(KRB_6036));  // open: Y3, Y7
  _74LS238 _74ls238_5 (
    .A(IR[0]), .B(IR[1]), .C(IR[2]), .G(IOT_TTYPUNCH), .nGB(1'b0), .nGA(1'b0), .Y0(L_PRN[5]), .Y1(L_PRN[4]),
    .Y2(L_PRN[3]), .Y4(L_PRN[2]), .Y5(L_PRN[1]), .Y6(L_PRN[0]));  // open: Y3, Y7
  SequencerAI sequencerai_1 (
    .EN(or_65_out), .CLK(CLK_t), .fAI(fAutoinc), .DONE(ii), .P1a(enRAMtoDBUS_ai), .P1b(enINSTRtoABUS_ai),
    .P2(ckIncDBUS__ai), .P3a(weRAM_ai), .P3b(enIncToDBUS_ai), .Fin(aiFinished));
  Sequencer AND_TAD (
    .EN(and_50_out), .CLK(CLK_t), .DONE(ckACC_2), .D1(enRAMtoDBUS_andtad), .P1(AND_TAD_p1), .P2(AND_TAD_p2),
    .D3(AND_TAD_d3), .P3(AND_TAD_p3), .D4(AND_TAD_d4), .P4(AND_TAD_p4), .D5(AND_TAD_d5), .P5(AND_TAD_p5),
    .D6(AND_TAD_d6), .P6(AND_TAD_p6), .D7(enALUtoACC_andtad), .P7(AND_TAD_p7), .D8(ckACC_2));  // open: D2
  Sequencer u_DCA (
    .EN(and_51_out), .CLK(CLK_t), .DONE(ii_dca), .D1(DCA_d1), .P1(DCA_p1), .D2(DCA_d2), .P2(DCA_p2),
    .D3(DCA_d3), .P3(DCA_p3), .D4(DCA_d4), .P4(DCA_p4), .D5(DCA_d5), .P5(DCA_p5), .D6(enACCtoDBUS_dca),
    .P6(weRAM_dca), .D7(enACCclear_dca), .P7(DCA_p7), .D8(ii_dca));
  Sequencer JMP_JMPi (
    .EN(and_52_out), .CLK(CLK_t), .DONE(ii_jmp), .D1(enRAMtoDBUS_jmp), .P1(JMP_JMPi_p1), .D2(JMP_JMPi_d2),
    .P2(JMP_JMPi_p2), .D3(JMP_JMPi_d3), .P3(JMP_JMPi_p3), .D4(JMP_JMPi_d4), .P4(JMP_JMPi_p4),
    .D5(JMP_JMPi_d5), .P5(JMP_JMPi_p5), .D6(JMP_JMPi_d6), .P6(JMP_JMPi_p6), .D7(ckSetPC_jmp),
    .P7(JMP_JMPi_p7), .D8(ii_jmp));
  Sequencer JMS_JMSi (
    .EN(and_53_out), .CLK(CLK_t), .DONE(ii_jms), .D1(enRAMtoDBUS_jms), .P1(JMS_JMSi_p1), .D2(JMS_JMSi_d2),
    .P2(JMS_JMSi_p2), .D3(JMS_JMSi_d3), .P3(ckIncPC_jms1), .D4(JMS_JMSi_d4), .P4(ckSetPC_jms),
    .D5(JMS_JMSi_d5), .P5(JMS_JMSi_p5), .D6(JMS_JMSi_d6), .P6(JMS_JMSi_p6), .D7(JMS_JMSi_d7),
    .P7(JMS_JMSi_p7), .D8(ii_jms));
  and and_54 (MOP3, IR[0], IR[8], L_GEN[4]);
  and and_55 (MOP2, not_30_out, IR[8], L_GEN[4]);
  and and_56 (MOP1, not_31_out, L_GEN[4]);
  nor nor_3 (nor_3_out, IOT, L_GEN[4]);
  and and_57 (ZEROPAGE, IR[7], nor_3_out);
  and and_58 (INDIRECT, IR[8], nor_3_out);
  and and_59 (and_59_out, enRAMtoDBUS_andtad, ~fIndirect);  // And
  and and_60 (and_60_out, JMP_JMPi_d2, ~fIndirect);  // And
  and and_61 (ckDBUStoABUS_jmp, JMP_JMPi_d2, fIndirect);
  and and_62 (enALUand, AND, enALUtoACC_andtad);
  and and_63 (enALUadd, L_GEN[10], enALUtoACC_andtad);
  and and_64 (and_64_out, DCA_d1, ~fIndirect);  // And
  or or_66 (enINSTRtoABUS_jmp, JMP_JMPi_p1, and_60_out);
  or or_67 (enINSTRtoABUS_andtad, and_59_out, AND_TAD_p1, AND_TAD_p2);
  and and_65 (ckDBUStoABUS_andtad, AND_TAD_p2, fIndirect);
  and and_66 (enDBUStoABUS_andtad, AND_TAD_d3, fIndirect);
  or or_68 (enRAMtoDBUS_dca, DCA_p1, DCA_p2, DCA_p3);
  or or_69 (enINSTRtoABUS_dca, and_64_out, DCA_p1, DCA_p2);
  and and_67 (ckDBUStoABUS_dca, DCA_p2, fIndirect);
  and and_68 (enDBUStoABUS_dca, DCA_d3, fIndirect);
  and and_69 (and_69_out, JMS_JMSi_d2, ~fIndirect);  // And
  and and_70 (ckDBUStoABUS_jms, JMS_JMSi_d2, fIndirect);
  // Probe on AND
  // Probe on L_GEN[10]
  // Probe on ISZ
  // Probe on DCA
  // Probe on JMS
  // Probe on JMP
  // Probe on IOT
  // Probe on L_GEN[4]
  or or_70 (enINSTRtoABUS_jms, JMS_JMSi_p1, and_69_out);
  // Probe on PC
  // Probe on IRA
  // Probe on ACC
  // Probe on ABUS
  // Probe on DAW[11:0]
  not not_32 (not_32_out, IR[3]);
  not not_33 (not_33_out, IR[4]);
  not not_34 (not_34_out, IR[5]);
  not not_35 (not_35_out, IR[6]);
  Sequencer ISZ_ISZi (
    .EN(ISZ), .CLK(CLK_t), .DONE(ii_isz), .D1(ISZ_ISZi_d1), .P1(ISZ_ISZi_p1), .P2(ISZ_ISZi_p2),
    .P3(ISZ_ISZi_p3), .D4(ISZ_ISZi_d4), .P5(ckIncDBUS_isz1), .P6(enIncToDBUS_isz1), .P7(INC1_isz), .D8(ii_isz));  // open: D2, D3, P4, D5, D6, D7
  and and_71 (IAC, MOP1, IR[0]);
  and and_72 (CML, MOP1, IR[4]);
  and and_73 (CMA, MOP1, IR[5]);
  and and_74 (CLL, MOP1, IR[6]);
  and and_75 (CLA_1, MOP1, IR[7]);
  and and_76 (CODE_lsb, MOP3, IR[1]);
  and and_77 (CODE_mid, MOP3, IR[2]);
  and and_78 (CODE_msb, MOP3, IR[3]);
  and and_79 (MQL, MOP3, IR[4]);
  and and_80 (SCA, MOP3, IR[5]);
  and and_81 (MQA, MOP3, IR[6]);
  and and_82 (CLA_3, MOP3, IR[7]);
  or or_71 (or_71_out, enIncToDBUS_isz1, enIncToDBUS_isz2);
  _74LS238 _74ls238_6 (
    .A(IR[1]), .B(IR[2]), .C(IR[3]), .G(MOP1), .nGB(1'b0), .nGA(1'b0), .Y1(BSW), .Y2(L_OPR1[1]),
    .Y3(L_OPR1[2]), .Y4(L_OPR1[4]), .Y5(L_OPR1[3]));  // open: Y0, Y6, Y7
  and and_83 (HLT, MOP2, IR[1]);
  and and_84 (L_OPR2[1], MOP2, IR[2]);
  and and_85 (L_OPR2[2], MOP2, IR[3], IR[4]);
  and and_86 (L_OPR2[4], MOP2, IR[3], IR[5]);
  and and_87 (L_OPR2[5], MOP2, IR[3], IR[6]);
  and and_88 (L_OPR2[3], MOP2, not_32_out, IR[4]);
  and and_89 (L_OPR2[6], MOP2, not_32_out, IR[5]);
  and and_90 (L_OPR2[7], MOP2, not_32_out, IR[6]);
  and and_91 (CLA_2, MOP2, IR[7]);
  and and_92 (L_OPR2[8], MOP2, IR[3], not_33_out, not_34_out, not_35_out);
  and and_93 (enRAMtoDBUS_isz, ISZ_ISZi_d1, ~or_71_out);  // And
  // Probe on ABUS
  // Probe on DAW[11:0]
  and and_94 (INC2_isz, INC1_isz, fDBUSisZero);
  and and_95 (and_95_out, ~fIndirect, ISZ_ISZi_d4);  // And
  and and_96 (ckDBUStoABUS_isz, ISZ_ISZi_d4, fIndirect);
  or or_72 (enINSTRtoABUS_isz, ISZ_ISZi_p1, ISZ_ISZi_p2, and_95_out, ISZ_ISZi_p3);
  and and_97 (ckIncDBUS__isz2, fAutoinc, ISZ_ISZi_p2);
  and and_98 (enIncToDBUS_isz2, fAutoinc, ISZ_ISZi_p3);
  or or_73 (ii, ii_mop1, ckACC_2, ii_jmp, ii_dca, ii_iot, ii_isz, ii_mop2, ii_mop3a, ii_mop3b, ii_mop3c, ii_mop3d, ii_jms, 1'b0, 1'b0);
  or or_74 (iDone, iDone1, ckIRQhandler);
  Sequencer u_MOP1 (
    .EN(MOP1), .CLK(CLK_t), .DONE(ii_mop1), .D1(enALUtoACC_mop1), .P1(MOP1_p1), .D2(ckACC_mop1),
    .P2(MOP1_p2), .D3(MOP1_d3), .P3(MOP1_p3), .D4(MOP1_d4), .P4(MOP1_p4), .D5(MOP1_d5), .P5(MOP1_p5),
    .D6(MOP1_d6), .P6(MOP1_p6), .D7(MOP1_d7), .P7(ii_mop1));  // open: D8
  RS_FF_AS rs_ff_as_4 (.S(ii), .R(iDone), .Q(inhibitIR));  // open: nQ
  // Probe on iDone
  or or_75 (INC1, ii_dca, ckACC_2, ckACC_mop1, INC1_mop2, INC1_mop3a, ckSetPC_jms, INC1_mop3b, INC1_mop3c, INC1_mop3d, INC1_iot, INC1_isz);
  or or_76 (INC2, INC2_mop2, INC2_isz, INC2_iot3, INC2_iot5, INC2_iot1, INC2_iot2, INC2_iot4);
  Sequencer u_MOP2 (
    .EN(MOP2), .CLK(CLK_t), .DONE(ii_mop2), .D1(enPCtoABUS_mop2), .P1(MOP2_p1), .D2(MOP2_d2), .P2(INC1_mop2),
    .D3(enALUtoACC_mop2), .P3(MOP2_p3), .D4(MOP2_d4), .P4(MOP2_p4), .D5(MOP2_d5), .P5(MOP2_p5), .D6(MOP2_d6),
    .P6(MOP2_p6), .D7(MOP2_d7), .P7(MOP2_p7), .D8(ii_mop2));
  and and_99 (and_99_out, ~MQL, ~MQA, MOP3);  // And
  and and_100 (and_100_out, MQL, ~MQA, MOP3);  // And
  and and_101 (and_101_out, ~MQL, MQA, MOP3);  // And
  and and_102 (and_102_out, MQA, MQL, MOP3);
  Sequencer MOP3___NOP_CLR (
    .EN(and_99_out), .CLK(CLK_t), .DONE(ii_mop3a), .D1(MOP3___NOP_CLR_d1), .P1(INC1_mop3a),
    .D2(MOP3___NOP_CLR_d2), .P2(MOP3___NOP_CLR_p2), .D3(MOP3___NOP_CLR_d3), .P3(MOP3___NOP_CLR_p3),
    .D4(MOP3___NOP_CLR_d4), .P4(MOP3___NOP_CLR_p4), .D5(MOP3___NOP_CLR_d5), .P5(MOP3___NOP_CLR_p5),
    .D6(MOP3___NOP_CLR_d6), .P6(MOP3___NOP_CLR_p6), .D7(MOP3___NOP_CLR_d7), .P7(MOP3___NOP_CLR_p7),
    .D8(ii_mop3a));
  Sequencer MOP3___MQL (
    .EN(and_100_out), .CLK(CLK_t), .DONE(ii_mop3b), .D1(MOP3___MQL_d1), .P1(INC1_mop3b), .D2(ckMQ_1),
    .P2(MOP3___MQL_p2), .D3(MOP3___MQL_d3), .P3(MOP3___MQL_p3), .D4(MOP3___MQL_d4), .P4(MOP3___MQL_p4),
    .D5(MOP3___MQL_d5), .P5(MOP3___MQL_p5), .D6(MOP3___MQL_d6), .P6(MOP3___MQL_p6), .D7(MOP3___MQL_d7),
    .P7(MOP3___MQL_p7), .D8(ii_mop3b));
  // Sequencer MOP3___MQA: pin names not known; wires that end beside it: and_101_out, CLK_t, ii_mop3c, INC1_mop3c, enACCtoDBUS_2, ckACC_4, ii_mop3c, MOP3___MQL_d5, MOP3___MQL_p5, MOP3___MQL_d6, MOP3___MQL_p6, MOP3___MQL_d7, MOP3___MQL_p7, MOP3___MQA_p14, MOP3___MQA_p15
  Sequencer MOP3___SWP (
    .EN(and_102_out), .CLK(CLK_t), .DONE(ii_mop3d), .D1(MOP3___MQA_p14), .P1(INC1_mop3d), .D2(CLA_4),
    .P2(MOP3___MQA_p15), .D3(ckACC_5), .P3(MOP3___SWP_p3), .D4(MOP3___SWP_d4), .P4(MOP3___SWP_p4),
    .D5(MOP3___SWP_d5), .P5(MOP3___SWP_p5), .D6(MOP3___SWP_d6), .P6(MOP3___SWP_p6), .D7(MOP3___SWP_d7),
    .P7(MOP3___SWP_p7), .D8(ii_mop3d));
  and and_103 (and_103_out, ~enIRQ, inhibitIR);  // And
  and and_104 (and_104_out, inhibitIR, enIRQ);
  and and_105 (and_105_out, fAccZero, IR[5]);
  and and_106 (and_106_out, ACC[11], IR[6]);
  and and_107 (and_107_out, LINK, IR[4]);
  Sequencer sequencer_1 (
    .EN(and_103_out), .CLK(CLK_t), .DONE(iDone1), .D1(enPCtoABUS_LoadIR), .P1(iDoneBeforeIRQ),
    .D2(sequencer_1_d2), .P2(ckIR_LoadIR), .D3(sequencer_1_d3), .P3(sequencer_1_p3), .D4(sequencer_1_d4),
    .P4(sequencer_1_p4), .D5(sequencer_1_d5), .P5(sequencer_1_p5), .D6(sequencer_1_d6), .P6(sequencer_1_p6),
    .D7(sequencer_1_d7), .P7(sequencer_1_p7), .D8(iDone1));
  Sequencer sequencer_2 (
    .EN(and_104_out), .CLK(CLK_t), .DONE(ckIRQhandler), .D1(sequencer_2_d1), .P1(weRAM_irq),
    .D2(sequencer_2_d2), .P2(sequencer_2_p2), .D3(sequencer_2_d3), .P3(clrPC_irq), .D4(enPCtoABUS_irq),
    .P4(sequencer_2_p4), .D5(sequencer_2_d5), .P5(ckIncPC_irq1), .D6(sequencer_2_d6), .P6(ckIR_irq),
    .D7(sequencer_2_d7), .P7(sequencer_2_p7), .D8(ckIRQhandler));
  or or_77 (or_77_out, L_OPR2[1], CLA_2);
  and and_108 (STOPSOON, MOP2_d5, HLT);
  or or_78 (or_78_out, and_105_out, and_106_out, and_107_out);
  or or_79 (or_79_out, sequencer_1_p3, weRAM_irq);
  and and_109 (INC2_mop2, INC1_mop2, fSkip);
  and and_110 (enALUor_mop2, enALUtoACC_mop2, L_OPR2[1]);
  and and_111 (ckACC_mop2, or_77_out, MOP2_p4);
  xor xor_15 (fSkip, or_78_out, IR[3]);
  and and_112 (enACCclear_mop3a, CLA, INC1_mop3a);
  and and_113 (and_113_out, CLA, INC1_mop3b);
  and and_114 (enACCclear_mop3c, CLA, INC1_mop3c);
  and and_115 (enACCclear_mop3d, CLA, INC1_mop3d);
  or or_80 (enACCclear_mop3b, and_113_out, MOP3___MQL_p2);
  Delay #(.delayTime(20)) delay_3 (.in(iDoneBeforeIRQ), .out(delay_3_out));
  RS_FF_AS rs_ff_as_5 (.S(INC1), .R(or_79_out), .Q(rs_ff_as_5_q));  // open: nQ
  RS_FF_AS rs_ff_as_6 (.S(INC2), .R(or_79_out), .Q(rs_ff_as_6_q));  // open: nQ
  OneShot oneshot_7 (.i(iDoneBeforeIRQ), .o(oneshot_7_o));
  OneShot oneshot_8 (.i(delay_3_out), .o(oneshot_8_o));
  or or_81 (enPCtoDBUS_irq, weRAM_irq, sequencer_2_p2);
  LED led_122 (.in(rs_ff_as_5_q));
  and and_116 (and_116_out, oneshot_7_o, rs_ff_as_5_q);
  and and_117 (and_117_out, oneshot_8_o, rs_ff_as_6_q);
  Sequencer u_IOT (
    .EN(IOT), .CLK(CLK_t), .DONE(ii_iot), .D1(IOT_d1), .P1(INC1_iot), .D2(IOT_d2), .P2(IOT_p2), .D3(IOT_d3),
    .P3(IOT_p3), .D4(IOT_d4), .P4(IOT_p4), .D5(IOT_d5), .P5(IOT_p5), .D6(IOT_d6), .P6(IOT_p6), .D7(IOT_d7),
    .P7(ii_iot));  // open: D8
  LED led_123 (.in(rs_ff_as_6_q));
  or or_82 (ckIncPC_LoadIR, and_116_out, and_117_out);
  // Probe on PC
  // Probe on IRA
  // Probe on ACC
  // Probe on ABUS
  // Probe on DAW[11:0]
  // Probe on L_CPU[7]
  // Probe on ION_6001
  // Probe on IOF_6002
  // Probe on L_CPU[4]
  // Probe on GTF_6004
  // Probe on L_CPU[2]
  // Probe on L_CPU[1]
  // Probe on CAF_6007
  // Probe on L_PRN[5]
  // Probe on L_PRN[4]
  // Probe on L_PRN[3]
  // Probe on L_PRN[2]
  // Probe on L_PRN[1]
  // Probe on L_PRN[0]
  // Probe on KCF_6030
  // Probe on KSF_6031
  // Probe on KCC_6032
  // Probe on KIE_6035
  // Probe on KRB_6036
  or or_83 (or_83_out, INC2_iot5, IOF_6002);
  or or_84 (or_84_out, fPRN, fKBD);
  and and_118 (INC2_iot5, L_CPU[7], fGIE, INC1_iot);
  and and_119 (and_119_out, ION_6001, INC1_iot);
  and and_120 (and_120_out, or_83_out, INC1_iot);
  and and_121 (INC2_iot4, L_CPU[4], fPendInt, INC1_iot);
  and and_122 (and_122_out, INC1_iot, GTF_6004);
  and and_123 (and_123_out, INC1_iot, L_CPU[2]);
  and and_124 (and_124_out, INC1_iot, L_CPU[1]);
  and and_125 (CAF, INC1_iot, CAF_6007);
  and and_126 (and_126_out, L_PRN[5], INC1_iot);
  and and_127 (INC2_iot2, L_PRN[4], fPRN, INC1_iot);
  and and_128 (and_128_out, L_PRN[3], INC1_iot);
  and and_129 (and_129_out, INC1_iot, L_PRN[2]);
  and and_130 (INC2_iot1, L_PRN[1], or_84_out, INC1_iot);
  and and_131 (and_131_out, L_PRN[0], INC1_iot);
  and and_132 (and_132_out, KCF_6030, INC1_iot);
  and and_133 (INC2_iot3, KSF_6031, fKBD, INC1_iot);
  and and_134 (enACCclear_iot1, KCC_6032, INC1_iot);
  and and_135 (and_135_out, KRS_6034, INC1_iot);
  and and_136 (KIE, KIE_6035, INC1_iot);
  and and_137 (KRB, KRB_6036, INC1_iot);
  and and_138 (and_138_out, KRB_6036, IOT_p2);
  LED led_124 (.in(fGIE));
  LED led_125 (.in(L_IRQ[5]));
  LED led_126 (.in(L_CPU[7]));
  LED led_127 (.in(ION_6001));
  LED led_128 (.in(L_PRN[4]));
  LED led_129 (.in(L_PRN[5]));
  LED led_130 (.in(KCF_6030));
  LED led_131 (.in(KSF_6031));
  or or_85 (or_85_out, and_119_out, RTF_INTEset);
  or or_86 (or_86_out, RTF_INTEclr, ckIRQhandler, and_120_out, CAF);
  not not_36 (not_36_out, and_122_out);
  not not_37 (not_37_out, and_122_out);
  or or_87 (or_87_out, KRB, and_135_out);
  LED led_132 (.in(fIrqDly));
  LED led_133 (.in(IOF_6002));
  LED led_134 (.in(L_PRN[3]));
  LED led_135 (.in(KCC_6032));
  not not_38 (not_38_out, not_37_out);
  not not_39 (not_39_out, not_38_out);
  or or_88 (or_88_out, and_129_out, and_131_out);
  LED led_136 (.in(enIRQ));
  LED led_137 (.in(L_CPU[4]));
  LED led_138 (.in(L_PRN[2]));
  LED led_139 (.in(KRS_6034));
  // Probe on iDoneBeforeIRQ
  RS_FF_AS INTE (.S(or_85_out), .R(or_86_out), .Q(fGIE), .nQ(INTE_nq));
  not not_40 (not_40_out, not_39_out);
  not not_41 (not_41_out, or_87_out);
  not not_42 (not_42_out, not_41_out);
  LED led_140 (.in(L_IRQ[2]));
  LED led_141 (.in(fKBD));
  LED led_142 (.in(GTF_6004));
  LED led_143 (.in(L_CPU[2]));
  LED led_144 (.in(L_PRN[1]));
  LED led_145 (.in(L_PRN[0]));
  LED led_146 (.in(KIE_6035));
  LED led_147 (.in(KRB_6036));
  D_FF_AS d_ff_as_1 (.Set(1'b0), .D(1'b1), .C(iDoneBeforeIRQ), .Clr(INTE_nq), .Q(d_ff_as_1_q));  // open: nQ
  not not_43 (not_43_out, not_40_out);
  not not_44 (ckACC_gtf, not_43_out);
  or or_89 (or_89_out, and_132_out, enACCclear_iot1, KRB, CAF);
  not not_45 (not_45_out, not_42_out);
  not not_46 (ckACC_iot1, not_45_out);
  LED led_148 (.in(fPRN));
  LED led_149 (.in(L_CPU[1]));
  D_FF_AS d_ff_as_2 (
    .Set(1'b0), .D(d_ff_as_1_q), .C(iDoneBeforeIRQ), .Clr(INTE_nq), .Q(d_ff_as_2_q), .nQ(d_ff_as_2_nq));
  and and_139 (RTF_linkSet, and_123_out, ACC[11]);
  and and_140 (RTF_linkClr, and_123_out, ~ACC[11]);  // And
  and and_141 (RTF_INTEclr, and_123_out, ACC[7]);
  and and_142 (RTF_INTEset, and_123_out, ~ACC[7]);  // And
  or or_90 (or_90_out, and_126_out, tty_1_txdone);
  or or_91 (or_91_out, and_128_out, CAF, and_131_out);
  LED led_150 (.in(CAF_6007));
  LED led_151 (.in(AND));
  RS_FF_AS PRN_FLAG (.S(or_90_out), .R(or_91_out), .Q(fPRN));  // open: nQ
  RS_FF_AS KBD_FLAG (.S(oneshot_9_o), .R(or_89_out), .Q(fKBD));  // open: nQ
  // Probe on PC
  // Probe on IRA
  // Probe on IR
  // Probe on ACC
  // Probe on ABUS
  // Probe on DAW[11:0]
  LED led_152 (.in(L_GEN[10]));
  and and_143 (and_143_out, KIE, ACC[0]);
  and and_144 (and_144_out, KIE, ~ACC[0]);  // And
  LED led_153 (.in(ISZ));
  LED led_154 (.in(DCA));
  and and_145 (enIRQ, d_ff_as_2_q, fPendInt, fGIE);
  and and_146 (fIrqDly, fGIE, d_ff_as_2_nq);
  // Probe on ACC
  LED led_155 (.in(JMS));
  or or_92 (or_92_out, CAF, and_143_out);
  RS_FF_AS TTY_IE (.S(or_92_out), .R(and_144_out), .Q(TTY_IE_q));  // open: nQ
  LED led_156 (.in(JMP));
  and and_147 (and_147_out, TTY_IE_q, fPRN);
  TTY tty_1 (
    .ck(clk), .Tx(ACC), .TxTrig(or_88_out), .RxAck(and_138_out), .RxEn(or_87_out), .TxDone(tty_1_txdone),
    .Rx(ALU_out), .RxAvail(tty_1_rxavail));
  PullDown pulldown_18 (.out(L_IRQ[2]));
  PullDown pulldown_19 (.out(L_IRQ[5]));
  RAMSPY ramspy_4 (.Trig({12{1'b0}}), .DAW({DAW[24], ABUS, DAW[11:0]}), .O(ramspy_4_o));
  RAMSPY ramspy_5 (.Trig(12'h2), .DAW({DAW[24], ABUS, DAW[11:0]}), .O(ramspy_5_o));
  LED led_157 (.in(IOT));
  LED led_158 (.in(L_GEN[4]));
  _74LS244 _74ls244_9 (
    ._1A1(1'b0), ._1A2(1'b0), ._1A3(1'b0), ._1A4(1'b0), ._1nG(not_36_out), ._2A1(1'b0), ._2A2(1'b0),
    ._2A3(1'b0), ._2A4(fGIE), ._2nG(not_36_out), ._1Y1(ALU_out[0]), ._1Y2(ALU_out[1]), ._1Y3(ALU_out[2]),
    ._1Y4(ALU_out[3]), ._2Y1(ALU_out[4]), ._2Y2(ALU_out[5]), ._2Y3(ALU_out[6]), ._2Y4(ALU_out[7]));
  _74LS244 _74ls244_10 (
    ._1A1(1'b0), ._1A2(fPendInt), ._1A3(1'b0), ._1A4(LINK), ._1nG(not_36_out), ._2A1(LINK), ._2A2(1'b0),
    ._2A3(1'b0), ._2A4(1'b0), ._2nG(not_36_out), ._1Y1(ALU_out[8]), ._1Y2(ALU_out[9]), ._1Y3(ALU_out[10]),
    ._1Y4(ALU_out[11]), ._2Y1(ALU_Lout));  // open: _2Y2, _2Y3, _2Y4
  // Probe on ramspy_4_o
  // Probe on ramspy_5_o
  LED led_159 (.in(L_GEN[3]));
  // Probe on ALU_out
  and and_148 (and_148_out, tty_1_rxavail, _25Hz);
  LED led_160 (.in(fIndirect));
  or or_93 (fPendInt, and_147_out, fKBD);
  OneShot oneshot_9 (.i(and_148_out), .o(oneshot_9_o));
  LED led_161 (.in(fAutoinc));
  LED led_162 (.in(isCurrPage));

  // Other names for the same wires on the sheet: L_GEN (some bits) = {AND, ISZ, DCA, JMS, JMP, IOT, fIndirect, fAutoinc, isCurrPage};
  //   IR0__6[6:0] = IR[6:0]; OPR_TSTINV = IR[3]; OPR_SNLSZL = IR[4]; OPR_SZASNA = IR[5]; OPR_SMASPA = IR[6];
  //   DBUS[11:0] = DAW[11:0]; DAW[23:12] = ABUS; fAccNegative = ACC[11];
  //   L_OPR1 (some bits) = {CLA_1, CLL, CMA, CML, IAC, BSW};
  //   L_CPU (some bits) = {ION_6001, IOF_6002, GTF_6004, CAF_6007}; INC1_mop1 = ckACC_mop1; ckMQ_2 = ckACC_5;
  //   INC1_jms = ckSetPC_jms; L_OPR2 (some bits) = {CLA_2, HLT}; CLKA = MAX; L2 = enACCtoABUS;
  //   enDBUStoABUS_isz = ckDBUStoABUS_isz; enDBUStoABUS_jmp = ckDBUStoABUS_jmp; enDBUStoABUS_jms = ckDBUStoABUS_jms;
  //   L_IRQ (some bits) = {fGIE, fIrqDly, enIRQ, fKBD, fPRN}; enALUor_2 = enACCtoDBUS_2; enALUtoACC_4 = enACCtoDBUS_2;
  //   enMQtoOBUS_1 = enACCtoDBUS_2; enALUor_3 = CLA_4; enALUtoACC_5 = CLA_4; enMQhold = CLA_4; enMQtoOBUS_2 = CLA_4;
  //   enRAMtoDBUS_0 = ckSetPC_0; enRAMtoDBUS_irq = enPCtoABUS_irq; enRAMtoDBUS_LoadIR = enPCtoABUS_LoadIR;
  //   enSwitchToOBUS = enALUor_mop2; iDone2 = ckIRQhandler; ii_andtad = ckACC_2; INC1_tadand = ckACC_2;
  //   INC1_dca = ii_dca; L_KBD[5:0] = {KCF_6030, KSF_6031, KCC_6032, KRS_6034, KIE_6035, KRB_6036}; MOP = L_GEN[4];
  //   OSR = L_OPR2[1]; RAL = L_OPR1[1]; RAR = L_OPR1[4]; RTF_6005 = L_CPU[2]; RTL = L_OPR1[2]; RTR = L_OPR1[3];
  //   SGT_6006 = L_CPU[1]; SKON_6000 = L_CPU[7]; SKP = L_OPR2[8]; SMA = L_OPR2[7]; SNA = L_OPR2[4]; SNL = L_OPR2[3];
  //   SPA = L_OPR2[5]; SRQ_6003 = L_CPU[4]; SZA = L_OPR2[6]; SZL = L_OPR2[2]; TAD = L_GEN[10]; TCF_6042 = L_PRN[3];
  //   TFL_6040 = L_PRN[5]; TLS_6046 = L_PRN[0]; TPC_6044 = L_PRN[2]; TSF_6041 = L_PRN[4]; TSK_6045 = L_PRN[1];
  //   weRAM_isz1 = enIncToDBUS_isz1; weRAM_isz2 = enIncToDBUS_isz2; enPCtoDBUS_jms = ckIncPC_jms1;
  //   weRAM_jms = ckIncPC_jms1

  // Notes on the sheet:
  //   MAX: Hz: 2147483647
  //   SWITCH: default 4095
  //   _25Hz: Hz: 200
  //   in_4: default 1920
  //   clk: Hz: 50
  //   DBUS ADDER
  //   DBUS->ABUS LATCH
  //   ADDRESS FROM INSTRUCTION
  //   SWITCH
  //   RAM
  //   PROGRAM COUNTER
  //   ACCUMULATOR / LINK
  //   contents of eeprom_1 (hex, n*v repeats v):
  //   120*8080,42,140,32c,32c,316,400,b00,1,34,0,0,0,3823,f19,0,23c
  //   ,d1a,0,0,714,0,0,0,100,0,0,301f,0,0,0,3823,11*0,336,410,1437,0,0,0
  //   ,303f,301f,2c0b,c14,3e16,3616,100,d02,0,500,0,c02,702,302,1f03
  //   ,a02,d02,23c,3f,2e02,13f,3e,303f,3f01,f00,3f02,3e3f,3f3c,3002
  //   ,203d,123d,333d,3d3f,3b3f,373f,3f00,2,20,1810,2d11,d2f,30,32,2019
  //   ,61a,2019,f1a,f10,714,1105,350d,3f04,1c05,2c05,3c12,215,c0b,1107
  //   ,3514,2d11,1514,203,2212,3013,b04,f0d,1b0d,1d10,2407,7,3210,1617
  //   ,3e41,3923,83e,42,3e2d,1f09,1218,138,19,1618,160a,b18,150a,2925
  //   ,1a09,818,3218,1a09,1718,2a25,2725,3b00,3c04,2625,f2a,2a02,101a
  //   ,2625,2625,1a09,f18,1018,2525,1d08,b18,3025,3125,322b,392a,1610
  //   ,2c25,1409,3508,203e,3625,3008,818,3218,3708,81c,3025,83c,2525
  //   ,2625,3608,e09,203e,302a,3525,2e25,3f29,2025,906,120c,283c,3f29
  //   ,1218,1208,138,1a2a,0,3025,3608,a09,283e,122b,1e18,3927,2708,3a03
  //   ,2608,203e,3625,2708,2f25,438,3718,3125,2525,3125,202b,2a2b,2c08
  //   ,639,2c08,438,3708,3718,2525,3125,3625,2a2b,2c08,3708,3718,2525
  //   ,3125,202b,83c,3625,39,3708,401,203e,1038,3708,601,303c,3625,203e
  //   ,3b0b,1038,438,3518,22f,2e,203f,10,c10,810,3009,2209,2b0d,230b
  //   ,28,1026,2028,52a,2a,3c,1517,1517,1517,0,639,638,638,b2e,2c25
  //   ,1208,2225,2325,f00,2325,3500,3508,83f,332a,2d25,38,1308,918,90c
  //   ,3325,3625,2025,606,2425,3500,120c,283c,392a,138,1818,3508,203f
  //   ,302a,180c,3325,392a,180c,3718,152a,2d25,3625,2025,806,2425,3500
  //   ,2425,f00,b0c,1218,3e2e,906,0,3918,2038,823,3908,b1c,2038,823
  //   ,3f2e,0,b08,b18,b08,2139,1908,183e,3625,82f,0,110f,3918,2038,823
  //   ,110b,138,b1c,2038,823,392c,0,203a,1c0f,918,1c13,f09,823,f09,3918
  //   ,90c,b1c,3910,252b,f09,823,1c2f,0,203a,2c0f,2c13,918,f09,3918
  //   ,b0c,91c,3910,332b,2c2f,2017,a02,f02,1702,3d08,1f09,1517,3508
  //   ,46,806,c06,3a3c,2c25,2d25,3625,1308,1218,2525,3608,e09,283e,212d
  //   ,2825,3e0b,82a,3608,3d00,2225,2525,2825,3e0b,83c,132a,b0c,2725
  //   ,3b07,3701,3625,2c25,1610,2d25,372a,3708,203e,2b25,2525,2925,3608
  //   ,e09,203e,242a,130c,283c,392a,138,1818,3508,3f,180c,3325,3b2a
  //   ,180c,3718,1f2a,1308,2b2a,1618,212d,3508,283f,392a,2925,342a,0
  //   ,3025,2825,370f,2f,3608,13,20a,283e,f2b,3125,2f,83c,2f,13,13,2f
  //   ,0,110f,a18,a0c,83d,202b,2138,3608,203e,142b,110f,2038,a08,2c18
  //   ,83c,1113,1113,3b,112f,0,401,2138,3918,3708,401,3908,283e,2413
  //   ,242f,0,1e08,203e,342b,2525,2e2f,2a25,2725,3e37,21c,2e2f,1d08
  //   ,806,c06,1303,603,903,403,48,703,303,103,1403,c03,503,1703,d03
  //   ,1103,1203,a02,3425,1f26,b10,2026,909,1a18,2508,83d,1a10,283f
  //   ,1a10,83c,372f,2725,3f0b,393b,2525,182a,2525,152a,10e,2710,2025
  //   ,30c,3025,3608,1d0b,203c,3625,1808,2225,2025,a0e,b0c,1818,724
  //   ,1834,0,2725,3f0b,3f39,3625,1808,2225,2025,a0e,2725,3f0b,3c39
  //   ,3625,2325,1810,2025,a0e,2325,1810,2325,f00,2025,806,2425,f00
  //   ,2425,1810,2425,383c,b0c,1818,724,1804,1b0f,1834,1515,0,2508,203f
  //   ,212d,1808,2225,2325,383c,12b,33d,143d,2325,514,12b,2b24,2225
  //   ,3608,1e0b,203e,3625,2025,a0e,2b24,3330,3a,b0c,2f30,83c,2b24,3a
  //   ,1e2d,2108,2108,b08,1004,306,c06,20a,30a,33d,412,1d06,2e0a,3f01
  //   ,4a,330d,3133,203a,2e18,1618,2725,390b,3e01,2e10,162a,2025,30c
  //   ,3608,2225,2d0a,2925,1e10,138,1925,b0c,3618,22a,2025,b0e,1825
  //   ,32a,1610,2525,2725,30c,3b07,2925,1b2a,2525,2c25,3708,2a18,42a
  //   ,3f08,3324,2038,3f08,2925,2525,42a,3a02,2c25,2d25,3625,3008,818
  //   ,3218,3708,81c,808,1718,3424,19,1610,2525,2925,2725,3e00,390a
  //   ,2625,3b2a,3008,138,818,3218,2a25,2725,3900,390a,2625,62b,0,283c
  //   ,3608,2138,3918,c0f,c13,a18,a0c,83d,202b,3908,203e,142b,a08,c0f
  //   ,3918,390c,3918,392c,c13,3b,c2f,2b24,38,3d33,1a33,262b,3233,2618
  //   ,130,1e2d,0,2630,1630,2130,2f2b,3a,2c2f,3b0a,380a,2017,20b,390a
  //   ,3102,a0b,2502,2202,2102,2302,2402,2002,4c,2c02,3b02,d02,3425
  //   ,2202,d02,3625,3218,2625,2525,2825,370f,162a,3608,1201,3108,3118
  //   ,2525,2825,370f,162a,112a,3225,1f2a,3108,2e18,3026,b0c,3118,2f26
  //   ,2b24,f1b,3008,1818,1808,2138,1908,283f,312a,180c,2138,3108,283e
  //   ,52b,1808,3808,212a,2710,10e,1908,508,2139,b08,103e,3625,1908
  //   ,3808,1918,3108,181c,1810,f0b,181c,1810,724,1f05,1834,0,212d,1808
  //   ,918,90c,2138,f0b,203e,2c2a,1810,1810,212d,0,3608,c09,203e,f2f
  //   ,2525,102b,103d,73d,0,10,0,0,3608,d09,203e,1b13,3608,160b,2c18
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  //   INSTRUCTIONS PER SECOND
  //   INSTRUCTION REGISTER
  //   Latch at rising C
  //   RUN/STEP CLOCK
  //   PC
  //   MQ
  //   OPCODES
  //   OPR-3
  //   OPR-2
  //   OPR-1
  //   TAD
  //   AND
  //   NOP
  //   CLA
  //   SKP
  //   ISZ
  //   SCA
  //   SMA
  //   CLL
  //   contents of CharRom3x (hex, n*v repeats v):
  //   128*483f24cc03cf,128*1483f24cc03cf,128*2483f24cc03cf,128*3483f24cc03cf
  //   ,128*483f03cf4803,128*1483f03cf4803,128*2483f03cf4803,128*3483f03cf4803
  //   ,128*903303bb4833,128*1903303bb4833,128*2903303bb4833,128*3903303bb4833
  //   ,128*3cf00f3483f,128*103cf00f3483f,128*203cf00f3483f,128*303cf00f3483f
  //   ,128*3bb14cc007c,128*103bb14cc007c,128*203bb14cc007c,128*303bb14cc007c
  //   ,128*3c714cc007c,128*103c714cc007c,128*203c714cc007c,128*303c714cc007c
  //   ,513*480300ff4833,257*3c700ff14cc,0,253*3c700ff14cc
  //   CODE1
  //   DCA
  //   SWP
  //   SZA
  //   CMA
  //   CODE2
  //   JMS
  //   JMP
  //   MQA
  //   MQL
  //   SNA
  //   SPA
  //   IAC
  //   CML
  //   INTERRUPT FLAGS
  //   GIE
  //   IOT-CPU
  //   SKON
  //   IOT-PRINTER
  //   TFL
  //   IOT-KEYBOARD
  //   KCF
  //   IR
  //   CODE3
  //   IOT
  //   LSR
  //   SNL
  //   RAR
  //   IRQ
  //   INH
  //   ION
  //   TSF
  //   KSF
  //   OPR
  //   ASL
  //   SZL
  //   RTR
  //   IRQ
  //   DLY
  //   IRQ
  //   IOF
  //   SRQ
  //   TCF
  //   TPC
  //   KCC
  //   KRS
  //   DIR
  //   IND
  //   SHL
  //   NMI
  //   OSR
  //   HLT
  //   RAL
  //   RTL
  //   TTY
  //   IE
  //   GTF
  //   TSK
  //   KIE
  //   AUTO
  //   IND
  //   DVI
  //   BSW
  //   KEY
  //   AVAIL
  //   RTF
  //   TLS
  //   KRB
  //   CURR
  //   PAGE
  //   MUY
  //   PRN
  //   RDY
  //   SGT
  //   CAF
  //   SCL
  //   ABUS
  //   DBUS
  //   ACC
  //   IRQ
  //   IHBT
  //   INT
  //   BUS
  //   ALU
  //   OBUS
  //   ADD
  //   IAC
  //   SEQ OPR 1 MICROCODES
  //   ------------------------------------
  //   1 CLA CLL
  //   2 CMA CML
  //   3 IAC
  //   4 RAR RAL RTR RTL BSW
  //   RAR
  //   RAL
  //   RTR
  //   RTL
  //   BSW
  //   PASSTHRU
  //   SWAP
  //   ROT L1
  //   ROT L2
  //   ROT R1
  //   ROT R2
  //   INSTRUCTION DECODER
  //   AND/ADD Accumulator
  //   deposit and clear AC
  //   GRP3 msb1 & lsb1
  //   GRP2 msb1 & lsb0
  //   GRP1 msb0
  //   MOP DECODER
  //   increment and skip if zero
  //   MOPGRP1
  //   IR LOAD & PC INCREMENTER
  //   AC negative
  //   LINK<>0
  //   load MQ from AC then clear AC
  //   inclusive OR the MQ with the AC
  //   AC=0
  //   SMA      7500  skip on minus AC
  //   SPA      7510  skip on plus AC
  //   SZA      7440  skip on zero AC
  //   SNA      7450  skip on non-zero AC
  //   SNL      7420  skip on non-zero link
  //   SZL      7430  skip on zero link
  //   IOT - CPU IRQ
  //   IOT - TELEPRINTER
  //   IOT - KEYBOARD
  //   Keyboard Flag
  //   The keyboard flag bit is set when a character has been read into the keyboard buffer. The console-reset or 
  //   power-on operation clears this flag. If interrupts are enabled, this flag generates an interrupt request when set.
  //   Teleprinter Flag
  //   The teleprinter flag bit is set when the character most recently loaded in the teleprinter buffer has been output. 
  //   The console-reset or power-on operation clears this flag. If interrupts are enabled, this flag generates an interrupt 
  //   request when set.
  //   -------------------------------------------------------------------------------------------------------------------------------------------------
  //   6000 - SKON Skip if Interrupt System On
  //   SKON is used to test the state of the interrupt enable flipflop. If interrupts are enabled, the next instruction in sequence is skipped.
  //   6001 - ION Interrupts On
  //   ION is used to turn on interrupts. The effect of this instruction is delayed one instruction so that, for example, an ION instruction 
  //   immediately before a return instruction will not take effect until the return instruction is executed.
  //   6002 - IOF Interrupts Off
  //   IOF is used to turn off or disable interrupts. The effect of this instruction is immediate. In addition, interrupts are disabled immediately 
  //   when an interrupt occurs.
  //   6003 - SRQ Skip on Interrupt Request
  //   SRQ is used to test whether there is a pending interrupt request. If a request is pending, the next instruction in sequence is skipped. 
  //   This test is only meaningful when interrupts are disabled; it may be used, for example, to avoid the expense of an unnecessary return 
  //   from interrupt when some device other than the one just serviced is also requesting service.
  //   6004 - GTF Get Flags
  //   GTF is similar to RIB, but is only available on the PDP-8/E and later models. 
  //   GTF loads the accumulator with various information that may need to be saved and restored during interrupts. 
  //   This includes the link bit, the state of the optional memory management unit, and the greater-than flag from 
  //   the optional extended arithmetic unit. These are packed into the accumulator in the following format:
  //   LINK- the link bit.
  //   GT - the Greater Than bit (see the SGT instruction supported by the extended arithmetic element.
  //   IR - the interrupt request status, as tested by SRQ. This is set to one if an interrupt requesting is pending.
  //   II - the interrupt inhibit bit associated with the Time-Share option of the memory management unit.
  //   IE - the state of the interrupt enable flipflop, as set by the ION and reset by the IOF instructions. This is set to one if interrupts are enabled.
  //   U - the user-mode bit.
  //   IF - the instruction field.
  //   DF - the data field. 
  //   U, IF and DF are the same as the corresponding fields returned by the RIB instruction.
  //   6005 - RTF Restore Flags
  //   RTF restores the state of the flags that are saved by the GTF instruction, using the same data format. 
  //   RTF ignores the IR (interrupt request) bit that was saved by GTF, and the IE (interrupt enable) bit is not fully restored until the 
  //   instruction after the RTF instruction, so that a return from interrupt may be executed before the next interrupt request is serviced.
  //   6006 - SGT Skip if Greater Than
  //   SGT is only supported if the extended arithmetic element is present, This instruction skips if the greater than flag is set.
  //   6007 - CAF Clear All Flags
  //   The effect of the CAF instruction is identical to a master clear issued from the front panel. AC and LINK are cleared, interrupts 
  //   are disabled globally, and all I/O devices are reset. Generally, resetting a device sets the device specific interrupt enable bit 
  //   and terminates any ongoing I/O activity. 
  //   -------------------------------------------------------------------------------------------------------------------------------------------------
  //   6030 - KCF Keyboard Clear Flags
  //   The keyboard flag, signalling input data ready, is cleared.
  //   6031 - KSF Keyboard Skip if Flag
  //   If the keyboard flag is set, indicating that input data is ready, the next instruction in sequence is skipped. 
  //   6032 - KCC Keyboard Clear and read character
  //   The keyboard flag is reset, the accumulator is cleared, and the process of reading the next character of input 
  //   is initiated (in those cases where the interface is connected to a paper-tape reader).
  //   6034 - KRS Keyboard Read Static
  //   The 8-bit character in the keyboard buffer is ored with the accumulator.
  //   6035 - KIE Keyboard Interrupt Enable
  //   The accumulator is loaded into the device control register (the interrupt enable and status report control bits). 
  //   6036 - KRB Keyboard Read and begin next read
  //   The 8 bit character in the keyboard buffer is transferred to the accumulator, and the keyboard flag is cleared, 
  //   allowing the reading of the next character to begin. In effect, this operation combines the KCC and KRS operations.
  //   -------------------------------------------------------------------------------------------------------------------------------------------------
  //   6040 - TFL Teleprinter Flag set
  //   The printer flag, signalling output complete, is set. 
  //   6041 - TSF Teleprinter Skip if Flag
  //   If the printer flag is set, indicating output is complete, the next instruction in sequence is skipped. 
  //   6042 - TCF Teleprinter Clear Flag
  //   The printer flag is reset.
  //   6044 - TPC Teleprinter Print Character
  //   The least significant 8-bits of the accumulator is copied to the print buffer, initiating output.
  //   6045 - TSK Teleprinter Skip
  //   If either the print flag or the keyboard flag are set, the next instruction in sequence is skipped. 
  //   6046 - TLS Teleprinter Load and start
  //   The least significant 8 bits of the accumulator are copied to the print buffer, initiating output, and the printer flag is reset. 
  //   In effect, this operation combines the TCF and TPC operations.
endmodule
