// Digital circuit TTY.dig as structural Verilog
module TTY (
  input  ck,
  input  [11:0] Tx,
  input  TxTrig,
  input  RxAck,
  input  RxEn,
  output TxDone,
  output [11:0] Rx,
  output RxAvail
);

  wire d_ff_as_1_q, d_ff_as_2_q, d_ff_as_3_q, d_ff_as_4_q, d_ff_as_5_q;
  wire [15:7] keyboard_1_d;

  Terminal terminal_1 (.D({1'b0, Tx[6:0]}), .C(TxTrig), .en(1'b1));
  Keyboard keyboard_1 (.C(RxAck), .en(RxEn), .D({keyboard_1_d, Rx[6:0]}), .av(RxAvail));
  D_FF_AS d_ff_as_1 (.Set(1'b0), .D(1'b1), .C(ck), .Clr(TxTrig), .Q(d_ff_as_1_q));  // open: nQ
  assign Rx[11:7] = RxEn ? 5'b00001 : 5'bz;  // Driver driver_1
  D_FF_AS d_ff_as_2 (.Set(1'b0), .D(d_ff_as_1_q), .C(ck), .Clr(TxTrig), .Q(d_ff_as_2_q));  // open: nQ
  D_FF_AS d_ff_as_3 (.Set(1'b0), .D(d_ff_as_2_q), .C(ck), .Clr(TxTrig), .Q(d_ff_as_3_q));  // open: nQ
  D_FF_AS d_ff_as_4 (.Set(1'b0), .D(d_ff_as_3_q), .C(ck), .Clr(TxTrig), .Q(d_ff_as_4_q));  // open: nQ
  D_FF_AS d_ff_as_5 (.Set(1'b0), .D(d_ff_as_4_q), .C(ck), .Clr(TxTrig), .Q(d_ff_as_5_q));  // open: nQ
  OneShot oneshot_1 (.i(d_ff_as_5_q), .o(TxDone));

  // Notes on the sheet:
  //   ck: Hz: 25
endmodule
